// Logisim project 8bit_not_lab.circ as structural Verilog: 1 circuit, main circuit comparator8bit
module comparator8bit (
  input  [7:0] A,
  output [7:0] out_2
);

  not not_1 (out_2[0], A[0]);
  not not_2 (out_2[1], A[1]);
  not not_3 (out_2[2], A[2]);
  not not_4 (out_2[3], A[3]);
  not not_5 (out_2[4], A[4]);
  not not_6 (out_2[5], A[5]);
  not not_7 (out_2[6], A[6]);
  not not_8 (out_2[7], A[7]);
endmodule
