// Logisim project equality.1980918.circ as structural Verilog: 2 circuits, main circuit equality
module main (
  input  in_1,
  input  in_2,
  output out_3
);

  wire and_1_out, and_2_out, not_1_out, not_2_out, or_1_out;

  not not_1 (not_1_out, in_1);
  not not_2 (not_2_out, in_2);
  and and_1 (and_1_out, not_1_out, in_2);
  and and_2 (and_2_out, in_1, not_2_out);
  or or_1 (or_1_out, and_1_out, and_2_out);
  not not_3 (out_3, or_1_out);
endmodule

module equality (
  input  [2:0] in_1,
  input  [2:0] in_2,
  output out_3
);

  wire main_1_out_3, main_2_out_3, main_3_out_3;

  main main_1 (.in_1(in_1[0]), .in_2(in_2[0]), .out_3(main_1_out_3));
  main main_2 (.in_1(in_1[1]), .in_2(in_2[1]), .out_3(main_2_out_3));
  main main_3 (.in_1(in_1[2]), .in_2(in_1[2]), .out_3(main_3_out_3));
  and and_1 (out_3, main_1_out_3, main_3_out_3);

  assign in_2[2] = in_1[2];
endmodule
