// Logisim project cpu_lab.circ as structural Verilog: 19 circuits, main circuit cpu_8bit
module cpu_8bit (
  input  Clr,
  input  Enable,
  output out_3,
  output out_4,
  output out_5,
  output out_6,
  output out_7,
  output out_8,
  output out_9,
  output out_10
);

  wire alu_8bit_1_eq, AlUenable, blockbottom_1_out_5, blockbottom_1_out_6, blockbottom_1_out_7,
       blockbottom_1_out_8, blockbottom_1_out_9, blockbottom_1_out_10, blockbottom_1_out_11,
       blockbottom_1_out_12, blockbottom_1_out_13, blockbottom_1_out_14, blockbottom_1_out_15,
       blockbottom_1_out_16, blockbottom_1_out_17, blockbottom_1_out_18, blockbottom_1_out_19,
       blockbottom_1_out_20, blockbottom_2_out_5, blockbottom_2_out_6, blockbottom_2_out_7,
       blockbottom_2_out_8, blockbottom_2_out_9, blockbottom_2_out_10, blockbottom_2_out_11,
       blockbottom_2_out_12, blockbottom_2_out_13, blockbottom_2_out_14, blockbottom_2_out_15,
       blockbottom_2_out_16, blockbottom_2_out_17, blockbottom_2_out_18, blockbottom_2_out_19,
       blockbottom_2_out_20, blocktop_1_out_5, blocktop_1_out_6, blocktop_1_out_7, blocktop_1_out_8,
       blocktop_1_out_9, blocktop_1_out_10, blocktop_1_out_11, blocktop_1_out_12, blocktop_1_out_13,
       blocktop_1_out_14, blocktop_1_out_15, blocktop_1_out_16, blocktop_1_out_17, blocktop_1_out_18,
       blocktop_1_out_19, blocktop_1_out_20, blocktop_2_out_5, blocktop_2_out_6, blocktop_2_out_7,
       blocktop_2_out_8, blocktop_2_out_9, blocktop_2_out_10, blocktop_2_out_11, blocktop_2_out_12,
       blocktop_2_out_13, blocktop_2_out_14, blocktop_2_out_15, blocktop_2_out_16, blocktop_2_out_17,
       blocktop_2_out_18, blocktop_2_out_19, blocktop_2_out_20, clock_1_out, Disp, Immsel, Inc, PCselbeq,
       PCseljmp, PCseljr, RAMload, RAMwrite, register_3_q, Regwrite;
  wire [1:0] Rdsel, register_2_q, register_4_q, Rxsel, WBDatsel;
  wire [3:0] Imm;
  wire [4:0] Addr;
  wire [7:0] adder_8bit_1_r, adder_8bit_2_r, alu_8bit_1_r, ALUCtrl, bit_extender_1_out, bit_extender_2_out,
       blackbox_1_out_5, blackbox_1_out_6, blackbox_1_out_7, blackbox_1_out_8, blackbox_2_out_5,
       blackbox_2_out_6, blackbox_2_out_7, blackbox_2_out_8, display_1_a, display_1_b, display_1_c,
       display_1_d, display_1_e, display_1_f, display_1_g, display_1_h, fetcher_1_romaddr, IR,
       multiplexer_1_out, multiplexer_2_out, multiplexer_3_out, NextPC, ram_1_dout, Regaddrin, register_1_q,
       registers_1_rd, rom_1_data;

  ROM rom_1 (.addr(fetcher_1_romaddr), .data(rom_1_data));
  Register #(.trigger("falling")) register_1 (.D(NextPC), .en(Enable), .clk(clock_1_out), .Q(register_1_q), .clr(Clr));
  Register #(.width(2), .trigger("falling")) register_2 (
    .D(WBDatsel), .en(Enable), .clk(clock_1_out), .Q(register_2_q), .clr(Clr));
  Register #(.width(1), .trigger("falling")) register_3 (
    .D(Regwrite), .en(Enable), .clk(clock_1_out), .Q(register_3_q), .clr(Clr));
  registers registers_1 (
    .Data(multiplexer_1_out), .Regwrite(register_3_q), .Rx(Regaddrin), .Rd(registers_1_rd), .Rdsel(Rdsel),
    .Rxsel(Rxsel), .Clock(clock_1_out), .Clear(Clr), .Rdwritereg(register_4_q));
  Multiplexer #(.select(2), .width(8), .enable("false")) multiplexer_1 (
    .in0(alu_8bit_1_r), .in1(ram_1_dout), .in2(adder_8bit_1_r), .in3(register_1_q), .out(multiplexer_1_out),
    .sel(register_2_q));
  Clock clock_1 (.out(clock_1_out));
  fetcher fetcher_1 (
    .Addr(Addr), .PCselbeq(PCselbeq), .Enable(Enable), .Clock(clock_1_out), .PCseljmp(PCseljmp),
    .Instruction(IR), .Eq(alu_8bit_1_eq), .ROMaddr(fetcher_1_romaddr), .ROMdata(rom_1_data), .Clr(Clr),
    .Regaddr(Regaddrin), .NextPC(NextPC), .PCseljr(PCseljr));
  adder_8bit adder_8bit_1 (.A(registers_1_rd), .B(8'h1), .R(adder_8bit_1_r), .Ctrl(Inc));  // open: Cout, Oflw
  adder_8bit adder_8bit_2 (.A(bit_extender_2_out), .B(Regaddrin), .R(adder_8bit_2_r), .Ctrl(Inc));  // open: Cout, Oflw
  assign bit_extender_1_out = {{4{1'b0}}, Imm};  // Bit_Extender bit_extender_1
  assign bit_extender_2_out = {{4{Imm[3]}}, Imm};  // Bit_Extender bit_extender_2
  Multiplexer #(.width(8), .enable("false")) multiplexer_2 (
    .in0(Regaddrin), .in1(bit_extender_1_out), .out(multiplexer_2_out), .sel(Immsel));
  Multiplexer #(.width(8), .enable("false")) multiplexer_3 (
    .in0(registers_1_rd), .in1(Regaddrin), .out(multiplexer_3_out), .sel(RAMwrite));
  alu_8bit alu_8bit_1 (
    .AluCtrl(ALUCtrl), .Enable(AlUenable), .A(multiplexer_2_out), .B(multiplexer_3_out), .R(alu_8bit_1_r),
    .ZF(out_7), .SF(out_8), .Oflw(out_9), .CF(out_10), .EQ(alu_8bit_1_eq));
  decoder decoder_1 (
    .IR(IR), .Aluctrl(ALUCtrl), .Rdsel(Rdsel), .Rxsel(Rxsel), .WBDatsel(WBDatsel), .PCselbeq(PCselbeq),
    .PCseljmp(PCseljmp), .RAMload(RAMload), .RAMwrite(RAMwrite), .Regwrite(Regwrite), .Addr(Addr),
    .Immsel(Immsel), .Imm(Imm), .Disp(Disp), .ALUenable(AlUenable), .PCjr(PCseljr), .Inc(Inc));
  RAM #(.trigger("falling"), .databus("bibus")) ram_1 (
    .addr(adder_8bit_2_r), .we(RAMwrite), .oe(RAMload), .clk(clock_1_out), .din(registers_1_rd),
    .dout(ram_1_dout));
  Register #(.width(2), .trigger("falling")) register_4 (
    .D(Rdsel), .en(Enable), .clk(clock_1_out), .Q(register_4_q), .clr(Clr));
  _7_Segment_Display u_7_segment_display_1 (
    .g(blocktop_1_out_5), .f(blocktop_1_out_13), .a(blocktop_1_out_14), .b(blocktop_1_out_6),
    .e(blockbottom_1_out_13), .d(blockbottom_1_out_5), .c(blockbottom_1_out_6), .dp(blockbottom_1_out_14));
  BlockBottom blockbottom_1 (
    .out_13(blockbottom_1_out_13), .out_5(blockbottom_1_out_5), .out_6(blockbottom_1_out_6),
    .out_14(blockbottom_1_out_14), .out_15(blockbottom_1_out_15), .out_7(blockbottom_1_out_7),
    .out_8(blockbottom_1_out_8), .out_16(blockbottom_1_out_16), .out_17(blockbottom_1_out_17),
    .out_9(blockbottom_1_out_9), .out_10(blockbottom_1_out_10), .out_18(blockbottom_1_out_18),
    .out_19(blockbottom_1_out_19), .out_11(blockbottom_1_out_11), .out_12(blockbottom_1_out_12),
    .out_20(blockbottom_1_out_20), .in_1(blackbox_1_out_5), .in_2(blackbox_1_out_6), .in_3(blackbox_1_out_7),
    .in_4(blackbox_1_out_8));
  BlockTop blocktop_1 (
    .in_1(blackbox_1_out_5), .in_2(blackbox_1_out_6), .in_3(blackbox_1_out_7), .in_4(blackbox_1_out_8),
    .out_5(blocktop_1_out_5), .out_13(blocktop_1_out_13), .out_14(blocktop_1_out_14),
    .out_6(blocktop_1_out_6), .out_7(blocktop_1_out_7), .out_15(blocktop_1_out_15),
    .out_16(blocktop_1_out_16), .out_8(blocktop_1_out_8), .out_9(blocktop_1_out_9),
    .out_17(blocktop_1_out_17), .out_18(blocktop_1_out_18), .out_10(blocktop_1_out_10),
    .out_11(blocktop_1_out_11), .out_19(blocktop_1_out_19), .out_20(blocktop_1_out_20),
    .out_12(blocktop_1_out_12));
  _7_Segment_Display u_7_segment_display_2 (
    .g(blocktop_1_out_7), .f(blocktop_1_out_15), .a(blocktop_1_out_16), .b(blocktop_1_out_8),
    .e(blockbottom_1_out_15), .d(blockbottom_1_out_7), .c(blockbottom_1_out_8), .dp(blockbottom_1_out_16));
  _7_Segment_Display u_7_segment_display_3 (
    .g(blocktop_1_out_9), .f(blocktop_1_out_17), .a(blocktop_1_out_18), .b(blocktop_1_out_10),
    .e(blockbottom_1_out_17), .d(blockbottom_1_out_9), .c(blockbottom_1_out_10), .dp(blockbottom_1_out_18));
  blackbox blackbox_1 (
    .out_5(blackbox_1_out_5), .out_6(blackbox_1_out_6), .out_7(blackbox_1_out_7), .out_8(blackbox_1_out_8),
    .in_1(display_1_a), .in_2(display_1_b), .in_3(display_1_c), .in_4(display_1_d));
  display display_1 (
    .in_2(registers_1_rd), .Dispwrite(Disp), .A(display_1_a), .B(display_1_b), .C(display_1_c),
    .D(display_1_d), .E(display_1_e), .F(display_1_f), .G(display_1_g), .H(display_1_h),
    .Display_select(Regaddrin[1:0]), .clock(clock_1_out), .reset(Clr));
  _7_Segment_Display u_7_segment_display_4 (
    .g(blocktop_1_out_11), .f(blocktop_1_out_19), .a(blocktop_1_out_20), .b(blocktop_1_out_12),
    .e(blockbottom_1_out_19), .d(blockbottom_1_out_11), .c(blockbottom_1_out_12), .dp(blockbottom_1_out_20));
  _7_Segment_Display u_7_segment_display_5 (
    .g(blocktop_2_out_5), .f(blocktop_2_out_13), .a(blocktop_2_out_14), .b(blocktop_2_out_6),
    .e(blockbottom_2_out_13), .d(blockbottom_2_out_5), .c(blockbottom_2_out_6), .dp(blockbottom_2_out_14));
  _7_Segment_Display u_7_segment_display_6 (
    .g(blocktop_2_out_7), .f(blocktop_2_out_15), .a(blocktop_2_out_16), .b(blocktop_2_out_8),
    .e(blockbottom_2_out_15), .d(blockbottom_2_out_7), .c(blockbottom_2_out_8), .dp(blockbottom_2_out_16));
  BlockBottom blockbottom_2 (
    .out_13(blockbottom_2_out_13), .out_5(blockbottom_2_out_5), .out_6(blockbottom_2_out_6),
    .out_14(blockbottom_2_out_14), .out_15(blockbottom_2_out_15), .out_7(blockbottom_2_out_7),
    .out_8(blockbottom_2_out_8), .out_16(blockbottom_2_out_16), .out_17(blockbottom_2_out_17),
    .out_9(blockbottom_2_out_9), .out_10(blockbottom_2_out_10), .out_18(blockbottom_2_out_18),
    .out_19(blockbottom_2_out_19), .out_11(blockbottom_2_out_11), .out_12(blockbottom_2_out_12),
    .out_20(blockbottom_2_out_20), .in_1(blackbox_2_out_5), .in_2(blackbox_2_out_6), .in_3(blackbox_2_out_7),
    .in_4(blackbox_2_out_8));
  BlockTop blocktop_2 (
    .in_1(blackbox_2_out_5), .in_2(blackbox_2_out_6), .in_3(blackbox_2_out_7), .in_4(blackbox_2_out_8),
    .out_5(blocktop_2_out_5), .out_13(blocktop_2_out_13), .out_14(blocktop_2_out_14),
    .out_6(blocktop_2_out_6), .out_7(blocktop_2_out_7), .out_15(blocktop_2_out_15),
    .out_16(blocktop_2_out_16), .out_8(blocktop_2_out_8), .out_9(blocktop_2_out_9),
    .out_17(blocktop_2_out_17), .out_18(blocktop_2_out_18), .out_10(blocktop_2_out_10),
    .out_11(blocktop_2_out_11), .out_19(blocktop_2_out_19), .out_20(blocktop_2_out_20),
    .out_12(blocktop_2_out_12));
  _7_Segment_Display u_7_segment_display_7 (
    .g(blocktop_2_out_9), .f(blocktop_2_out_17), .a(blocktop_2_out_18), .b(blocktop_2_out_10),
    .e(blockbottom_2_out_17), .d(blockbottom_2_out_9), .c(blockbottom_2_out_10), .dp(blockbottom_2_out_18));
  _7_Segment_Display u_7_segment_display_8 (
    .g(blocktop_2_out_11), .f(blocktop_2_out_19), .a(blocktop_2_out_20), .b(blocktop_2_out_12),
    .e(blockbottom_2_out_19), .d(blockbottom_2_out_11), .c(blockbottom_2_out_12), .dp(blockbottom_2_out_20));
  blackbox blackbox_2 (
    .out_5(blackbox_2_out_5), .out_6(blackbox_2_out_6), .out_7(blackbox_2_out_7), .out_8(blackbox_2_out_8),
    .in_1(display_1_e), .in_2(display_1_f), .in_3(display_1_g), .in_4(display_1_h));

  // Notes on the sheet:
  //   contents of rom_1 (hex, n*v repeats v):
  //   30 78 dd 61 d0 20 30 ff 20 30 77 d0 da c9
  //   Clock
  //   DISP[0]
  //   DISP[1]
  //   DISP[2]
  //   DISP[3]
endmodule

module alu_8bit (
  input  Enable,
  input  [7:0] AluCtrl,
  input  [7:0] A,
  input  [7:0] B,
  output [7:0] R,
  output ZF,
  output SF,
  output Oflw,
  output CF,
  output EQ
);

  wire adder_8bit_1_cout, adder_8bit_1_oflw, or_1_out;
  wire [7:0] adder_8bit_1_r, and_8bit_1_r, multiplexer_1_out, negator_1_out, or_8bit_1_r, shifter_8bit_1_r;

  and_8bit and_8bit_1 (.A(A), .B(B), .R(and_8bit_1_r));
  or_8bit or_8bit_1 (.A(A), .B(B), .R(or_8bit_1_r));
  adder_8bit adder_8bit_1 (
    .A(B), .B(A), .R(adder_8bit_1_r), .Cout(adder_8bit_1_cout), .Oflw(adder_8bit_1_oflw), .Ctrl(AluCtrl[5]));
  comparater_8bit comparater_8bit_1 (.out_3(EQ), .in_1(A), .in_2(B));
  shifter_8bit shifter_8bit_1 (.R(shifter_8bit_1_r), .X(A), .SUCtrl({Enable, AluCtrl[2:0]}));
  Negator negator_1 (.in(A), .out(negator_1_out));
  Multiplexer #(.select(2), .width(8), .enable("false")) multiplexer_1 (
    .in0(and_8bit_1_r), .in1(or_8bit_1_r), .in2(negator_1_out), .in3(A), .out(multiplexer_1_out),
    .sel(AluCtrl[4:3]));
  Multiplexer #(.select(2), .width(8)) multiplexer_2 (
    .in0({8{1'b0}}), .in1(multiplexer_1_out), .in2(adder_8bit_1_r), .in3(shifter_8bit_1_r), .out(R),
    .sel(AluCtrl[7:6]), .en(Enable));
  Multiplexer #(.select(2)) multiplexer_3 (
    .in0(1'b0), .in1(1'b0), .in2(adder_8bit_1_oflw), .in3(1'b0), .out(Oflw), .sel(AluCtrl[7:6]), .en(Enable));
  not not_1 (ZF, or_1_out);
  or or_1 (or_1_out, R[0], R[1], R[2], R[3], R[4], R[5], R[6], R[7]);
  Multiplexer #(.select(2)) multiplexer_4 (
    .in0(1'b0), .in1(1'b0), .in2(adder_8bit_1_cout), .in3(1'b0), .out(CF), .sel(AluCtrl[7:6]), .en(Enable));

  assign SF = R[7];

  // Notes on the sheet:
  //   Not
endmodule

module adder_1bit (
  input  Cin,
  input  A,
  input  B,
  output Result,
  output Cout
);

  wire and_1_out, and_2_out, xor_1_out;

  and and_1 (and_1_out, B, A);
  xor xor_1 (xor_1_out, A, B);
  and and_2 (and_2_out, xor_1_out, Cin);
  or or_1 (Cout, and_1_out, and_2_out);
  xor xor_2 (Result, Cin, xor_1_out);
endmodule

module adder_8bit (
  input  [7:0] A,
  input  Ctrl,
  input  [7:0] B,
  output [7:0] R,
  output Cout,
  output Oflw
);

  wire adder_1bit_1_cout, adder_1bit_2_cout, adder_1bit_3_cout, adder_1bit_4_cout, adder_1bit_5_cout,
       adder_1bit_6_cout, adder_1bit_7_cout, and_1_out, and_2_out, not_1_out, not_2_out, not_3_out,
       xor_1_out, xor_2_out, xor_3_out, xor_4_out, xor_5_out, xor_6_out, xor_7_out, xor_8_out;

  adder_1bit adder_1bit_1 (.A(A[0]), .B(xor_1_out), .Result(R[0]), .Cin(Ctrl), .Cout(adder_1bit_1_cout));
  xor xor_1 (xor_1_out, Ctrl, B[0]);
  adder_1bit adder_1bit_2 (.A(A[1]), .B(xor_2_out), .Result(R[1]), .Cin(adder_1bit_1_cout), .Cout(adder_1bit_2_cout));
  xor xor_2 (xor_2_out, Ctrl, B[1]);
  adder_1bit adder_1bit_3 (.A(A[2]), .B(xor_3_out), .Result(R[2]), .Cin(adder_1bit_2_cout), .Cout(adder_1bit_3_cout));
  xor xor_3 (xor_3_out, Ctrl, B[2]);
  adder_1bit adder_1bit_4 (.A(A[3]), .B(xor_4_out), .Result(R[3]), .Cin(adder_1bit_3_cout), .Cout(adder_1bit_4_cout));
  xor xor_4 (xor_4_out, Ctrl, B[3]);
  adder_1bit adder_1bit_5 (.A(A[4]), .B(xor_5_out), .Result(R[4]), .Cin(adder_1bit_4_cout), .Cout(adder_1bit_5_cout));
  xor xor_5 (xor_5_out, Ctrl, B[4]);
  adder_1bit adder_1bit_6 (.A(A[5]), .B(xor_6_out), .Result(R[5]), .Cin(adder_1bit_5_cout), .Cout(adder_1bit_6_cout));
  xor xor_6 (xor_6_out, Ctrl, B[5]);
  adder_1bit adder_1bit_7 (.A(A[6]), .B(xor_7_out), .Result(R[6]), .Cin(adder_1bit_6_cout), .Cout(adder_1bit_7_cout));
  xor xor_7 (xor_7_out, Ctrl, B[6]);
  adder_1bit adder_1bit_8 (.A(A[7]), .B(xor_8_out), .Result(R[7]), .Cin(adder_1bit_7_cout), .Cout(Cout));
  xor xor_8 (xor_8_out, Ctrl, B[7]);
  not not_1 (not_1_out, R[7]);
  not not_2 (not_2_out, xor_8_out);
  not not_3 (not_3_out, A[7]);
  and and_1 (and_1_out, not_1_out, xor_8_out, A[7]);
  and and_2 (and_2_out, R[7], not_2_out, not_3_out);
  or or_1 (Oflw, and_1_out, and_2_out);
endmodule

module and_8bit (
  input  [7:0] A,
  input  [7:0] B,
  output [7:0] R
);

  and and_1 (R[0], A[0], B[0]);
  and and_2 (R[1], A[1], B[1]);
  and and_3 (R[2], A[2], B[2]);
  and and_4 (R[3], A[3], B[3]);
  and and_5 (R[4], A[4], B[4]);
  and and_6 (R[5], A[5], B[5]);
  and and_7 (R[6], A[6], B[6]);
  and and_8 (R[7], A[7], B[7]);
endmodule

module or_8bit (
  input  [7:0] A,
  input  [7:0] B,
  output [7:0] R
);

  or or_1 (R[0], A[0], B[0]);
  or or_2 (R[1], A[1], B[1]);
  or or_3 (R[2], A[2], B[2]);
  or or_4 (R[3], A[3], B[3]);
  or or_5 (R[4], A[4], B[4]);
  or or_6 (R[5], A[5], B[5]);
  or or_7 (R[6], A[6], B[6]);
  or or_8 (R[7], A[7], B[7]);
endmodule

module shifter_8bit (
  input  [7:0] X,
  input  [3:0] SUCtrl,
  output [7:0] R
);

  wire multiplexer_1_out, multiplexer_3_out, multiplexer_5_out, multiplexer_6_out, multiplexer_9_out,
       multiplexer_11_out, multiplexer_13_out, multiplexer_14_out;

  Multiplexer #(.select(3), .enable("false")) multiplexer_1 (
    .in0(X[6]), .in1(X[3]), .in2(1'b0), .in3(1'b0), .in4(X[6]), .in5(X[3]), .in6(X[7]), .in7(X[7]),
    .out(multiplexer_1_out), .sel(SUCtrl[2:0]));
  Multiplexer #(.enable("false")) multiplexer_2 (.in0(X[7]), .in1(multiplexer_1_out), .out(R[7]), .sel(SUCtrl[3]));
  Multiplexer #(.select(3), .enable("false")) multiplexer_3 (
    .in0(X[5]), .in1(X[2]), .in2(X[7]), .in3(X[7]), .in4(X[5]), .in5(X[2]), .in6(X[7]), .in7(X[7]),
    .out(multiplexer_3_out), .sel(SUCtrl[2:0]));
  Multiplexer #(.enable("false")) multiplexer_4 (.in0(X[6]), .in1(multiplexer_3_out), .out(R[6]), .sel(SUCtrl[3]));
  Multiplexer #(.select(3), .enable("false")) multiplexer_5 (
    .in0(X[4]), .in1(X[1]), .in2(X[6]), .in3(X[6]), .in4(X[4]), .in5(X[1]), .in6(X[6]), .in7(X[6]),
    .out(multiplexer_5_out), .sel(SUCtrl[2:0]));
  Multiplexer #(.select(3), .enable("false")) multiplexer_6 (
    .in0(X[3]), .in1(X[0]), .in2(X[5]), .in3(X[5]), .in4(X[3]), .in5(X[0]), .in6(X[5]), .in7(X[5]),
    .out(multiplexer_6_out), .sel(SUCtrl[2:0]));
  Multiplexer #(.enable("false")) multiplexer_7 (.in0(X[5]), .in1(multiplexer_5_out), .out(R[5]), .sel(SUCtrl[3]));
  Multiplexer #(.enable("false")) multiplexer_8 (.in0(X[4]), .in1(multiplexer_6_out), .out(R[4]), .sel(SUCtrl[3]));
  Multiplexer #(.select(3), .enable("false")) multiplexer_9 (
    .in0(X[2]), .in1(1'b0), .in2(X[4]), .in3(X[4]), .in4(X[2]), .in5(1'b0), .in6(X[4]), .in7(X[4]),
    .out(multiplexer_9_out), .sel(SUCtrl[2:0]));
  Multiplexer #(.enable("false")) multiplexer_10 (.in0(X[3]), .in1(multiplexer_9_out), .out(R[3]), .sel(SUCtrl[3]));
  Multiplexer #(.select(3), .enable("false")) multiplexer_11 (
    .in0(X[1]), .in1(1'b0), .in2(X[3]), .in3(X[3]), .in4(1'b0), .in5(1'b0), .in6(X[3]), .in7(X[3]),
    .out(multiplexer_11_out), .sel(SUCtrl[2:0]));
  Multiplexer #(.enable("false")) multiplexer_12 (.in0(X[2]), .in1(multiplexer_11_out), .out(R[2]), .sel(SUCtrl[3]));
  Multiplexer #(.select(3), .enable("false")) multiplexer_13 (
    .in0(X[0]), .in1(1'b0), .in2(X[2]), .in3(X[2]), .in4(X[0]), .in5(1'b0), .in6(X[2]), .in7(X[2]),
    .out(multiplexer_13_out), .sel(SUCtrl[2:0]));
  Multiplexer #(.select(3), .enable("false")) multiplexer_14 (
    .in0(1'b0), .in1(1'b0), .in2(X[1]), .in3(X[1]), .in4(1'b0), .in5(1'b0), .in6(X[1]), .in7(X[1]),
    .out(multiplexer_14_out), .sel(SUCtrl[2:0]));
  Multiplexer #(.enable("false")) multiplexer_15 (.in0(X[1]), .in1(multiplexer_13_out), .out(R[1]), .sel(SUCtrl[3]));
  Multiplexer #(.enable("false")) multiplexer_16 (.in0(X[0]), .in1(multiplexer_14_out), .out(R[0]), .sel(SUCtrl[3]));
endmodule

module registers (
  input  [1:0] Rdwritereg,
  input  [1:0] Rdsel,
  input  [1:0] Rxsel,
  input  [7:0] Data,
  input  Regwrite,
  input  Clock,
  input  Clear,
  output [7:0] Rx,
  output [7:0] Rd
);

  wire demultiplexer_1_out0, demultiplexer_1_out1, demultiplexer_1_out2, demultiplexer_1_out3;
  wire [7:0] register_1_q, register_2_q, register_3_q, register_4_q;

  Demultiplexer #(.select(2), .enable("false")) demultiplexer_1 (
    .out0(demultiplexer_1_out0), .out1(demultiplexer_1_out1), .out2(demultiplexer_1_out2),
    .out3(demultiplexer_1_out3), .in(Regwrite), .sel(Rdwritereg));
  Register register_1 (.D(Data), .en(demultiplexer_1_out0), .clk(Clock), .Q(register_1_q), .clr(Clear));
  Register register_2 (.D(Data), .en(demultiplexer_1_out1), .clk(Clock), .Q(register_2_q), .clr(Clear));
  Register register_3 (.D(Data), .en(demultiplexer_1_out2), .clk(Clock), .Q(register_3_q), .clr(Clear));
  Register register_4 (.D(Data), .en(demultiplexer_1_out3), .clk(Clock), .Q(register_4_q), .clr(Clear));
  Multiplexer #(.select(2), .width(8), .enable("false")) multiplexer_1 (
    .in0(register_1_q), .in1(register_2_q), .in2(register_3_q), .in3(register_4_q), .out(Rx), .sel(Rxsel));
  Multiplexer #(.select(2), .width(8), .enable("false")) multiplexer_2 (
    .in0(register_1_q), .in1(register_2_q), .in2(register_3_q), .in3(register_4_q), .out(Rd), .sel(Rdsel));
endmodule

module comparater_8bit (
  input  [7:0] in_1,
  input  [7:0] in_2,
  output out_3
);

  wire not_1_out, not_2_out, not_3_out, not_4_out, not_5_out, not_6_out, not_7_out, not_8_out, xor_1_out,
       xor_2_out, xor_3_out, xor_4_out, xor_5_out, xor_6_out, xor_7_out, xor_8_out;

  xor xor_1 (xor_1_out, in_1[0], in_2[0]);
  xor xor_2 (xor_2_out, in_1[1], in_2[1]);
  xor xor_3 (xor_3_out, in_1[2], in_2[2]);
  xor xor_4 (xor_4_out, in_1[3], in_2[3]);
  xor xor_5 (xor_5_out, in_1[4], in_2[4]);
  xor xor_6 (xor_6_out, in_1[5], in_2[5]);
  xor xor_7 (xor_7_out, in_1[6], in_2[6]);
  xor xor_8 (xor_8_out, in_1[7], in_2[7]);
  not not_1 (not_1_out, xor_1_out);
  not not_2 (not_2_out, xor_2_out);
  not not_3 (not_3_out, xor_3_out);
  not not_4 (not_4_out, xor_4_out);
  not not_5 (not_5_out, xor_5_out);
  not not_6 (not_6_out, xor_6_out);
  not not_7 (not_7_out, xor_7_out);
  not not_8 (not_8_out, xor_8_out);
  and and_1 (out_3, not_1_out, not_2_out, not_3_out, not_4_out, not_5_out, not_6_out, not_7_out, not_8_out);
endmodule

module fetcher (
  input  Eq,
  input  PCselbeq,
  input  PCseljmp,
  input  PCseljr,
  input  Enable,
  input  [7:0] ROMdata,
  input  [4:0] Addr,
  input  [7:0] Regaddr,
  input  Clock,
  input  Clr,
  output [7:0] ROMaddr,
  output [7:0] NextPC,
  output [7:0] Instruction
);

  wire and_2_out;
  wire [7:0] adder_8bit_1_r, and_1_out, bit_extender_1_out, bit_extender_2_out, bit_extender_3_out,
       bit_extender_4_out, multiplexer_1_out, multiplexer_2_out, multiplexer_3_out, multiplexer_4_out,
       or_1_out;
  wire [7:7] not_1_out;

  not not_1 (not_1_out[7], 1'b0);
  assign bit_extender_1_out = {{7{1'b0}}, 1'b0};  // Bit_Extender bit_extender_1
  assign bit_extender_2_out = {{7{1'b0}}, not_1_out[7]};  // Bit_Extender bit_extender_2
  assign and_1_out = NextPC & {{3{not_1_out[7]}}, {5{1'b0}}};  // AND_Gate and_1, 8 bits wide
  assign bit_extender_3_out = {{3{Addr[4]}}, Addr};  // Bit_Extender bit_extender_3
  assign bit_extender_4_out = {{3{1'b0}}, Addr};  // Bit_Extender bit_extender_4
  Multiplexer #(.width(8), .enable("false")) multiplexer_1 (
    .in0(bit_extender_3_out), .in1(bit_extender_4_out), .out(multiplexer_1_out), .sel(PCseljmp));
  and and_2 (and_2_out, Eq, PCselbeq);
  Multiplexer #(.width(8), .enable("false")) multiplexer_2 (
    .in0(bit_extender_1_out), .in1(multiplexer_1_out), .out(multiplexer_2_out), .sel(and_2_out));
  assign or_1_out = multiplexer_1_out | and_1_out;  // OR_Gate or_1, 8 bits wide
  adder_8bit adder_8bit_1 (.A(multiplexer_2_out), .B(NextPC), .R(adder_8bit_1_r), .Ctrl(1'b0));  // open: Cout, Oflw
  Multiplexer #(.width(8), .enable("false")) multiplexer_3 (
    .in0(adder_8bit_1_r), .in1(or_1_out), .out(multiplexer_3_out), .sel(PCseljmp));
  Register #(.trigger("falling")) register_1 (.D(multiplexer_4_out), .en(Enable), .clk(Clock), .Q(ROMaddr), .clr(Clr));
  Multiplexer #(.width(8), .enable("false")) multiplexer_4 (
    .in0(multiplexer_3_out), .in1(Regaddr), .out(multiplexer_4_out), .sel(PCseljr));
  adder_8bit adder_8bit_2 (.A(ROMaddr), .B(bit_extender_2_out), .R(NextPC), .Ctrl(1'b0));  // open: Cout, Oflw
  Register register_2 (.D(ROMdata), .en(Enable), .clk(Clock), .Q(Instruction), .clr(Clr));
endmodule

module decoder (
  input  [7:0] IR,
  output [7:0] Aluctrl,
  output [1:0] Rdsel,
  output [1:0] Rxsel,
  output [1:0] WBDatsel,
  output Immsel,
  output PCselbeq,
  output PCseljmp,
  output PCjr,
  output RAMload,
  output RAMwrite,
  output Regwrite,
  output ALUenable,
  output Disp,
  output Inc,
  output [4:0] Addr,
  output [3:0] Imm
);

  wire and_3_out, and_4_out, decoder_1_out0, decoder_1_out1, decoder_1_out3, decoder_1_out6, decoder_2_out0,
       decoder_2_out1, decoder_2_out2, decoder_2_out3, decoder_2_out4, decoder_2_out5, decoder_2_out6,
       decoder_2_out7, not_1_out, not_2_out, or_7_out, or_8_out, or_11_out;
  wire [1:0] bit_extender_1_out, bit_extender_2_out, bit_extender_3_out, multiplexer_5_out, or_2_out,
       or_4_out, xor_1_out;
  wire [2:0] bit_extender_4_out;
  wire [3:0] multiplexer_7_out;
  wire [3:3] not_3_out;

  or or_1 (Rdsel[0], IR[4], PCselbeq);
  not not_1 (not_1_out, 1'b0);
  Multiplexer #(.select(3), .enable("false")) multiplexer_1 (
    .in0(1'b0), .in1(1'b0), .in2(not_1_out), .in3(1'b0), .in4(not_1_out), .in5(1'b0), .in6(IR[1]),
    .in7(1'b0), .out(Rxsel[1]), .sel(IR[7:5]));
  Multiplexer #(.select(3), .width(6), .enable("false")) multiplexer_2 (
    .in0({IR[0], IR[2:1], IR[2:0]}), .in1({IR[5], IR[7:6], IR[7:5]}), .in2({IR[5], IR[7:6], IR[7:5]}),
    .in3({IR[5], IR[7:6], IR[7:5]}), .in4({IR[5], IR[7:6], IR[7:5]}), .in5({IR[5], IR[7:6], IR[7:5]}),
    .in6({IR[5], IR[7:6], IR[7:5]}), .in7({IR[5], IR[7:6], IR[7:5]}), .out(Aluctrl[5:0]), .sel(IR[7:5]));
  Multiplexer #(.select(3), .enable("false")) multiplexer_3 (
    .in0(1'b0), .in1(1'b0), .in2(1'b0), .in3(1'b0), .in4(1'b0), .in5(1'b0), .in6(IR[2]), .in7(1'b0),
    .out(Rdsel[1]), .sel(IR[7:5]));
  and and_1 (Rxsel[0], IR[3], not_2_out);
  not not_2 (not_2_out, PCselbeq);
  assign bit_extender_1_out = {{1{1'b0}}, not_1_out};  // Bit_Extender bit_extender_1
  assign bit_extender_2_out = {{1{1'b0}}, 1'b0};  // Bit_Extender bit_extender_2
  assign bit_extender_3_out = {{1{1'b1}}, not_1_out};  // Bit_Extender bit_extender_3
  assign xor_1_out = bit_extender_1_out ^ bit_extender_3_out;  // XOR_Gate xor_1, 2 bits wide
  Multiplexer #(.select(3), .width(2), .enable("false")) multiplexer_4 (
    .in0(bit_extender_2_out), .in1(bit_extender_2_out), .in2(bit_extender_1_out), .in3(bit_extender_2_out),
    .in4(bit_extender_2_out), .in5(bit_extender_2_out), .in6(multiplexer_5_out), .in7(bit_extender_2_out),
    .out(WBDatsel), .sel(IR[7:5]));
  Multiplexer #(.select(3), .width(2), .enable("false")) multiplexer_5 (
    .in0(bit_extender_2_out), .in1(bit_extender_2_out), .in2(bit_extender_2_out), .in3(bit_extender_2_out),
    .in4(bit_extender_2_out), .in5(bit_extender_3_out), .in6(xor_1_out), .in7(xor_1_out),
    .out(multiplexer_5_out), .sel(IR[2:0]));
  Decoder #(.select(3), .enable("false")) decoder_1 (
    .out0(decoder_1_out0), .out1(decoder_1_out1), .out2(RAMload), .out3(decoder_1_out3), .out4(RAMwrite),
    .out5(PCseljmp), .out6(decoder_1_out6), .out7(PCselbeq), .sel(IR[7:5]));
  Decoder #(.select(3), .enable("false")) decoder_2 (
    .out0(decoder_2_out0), .out1(decoder_2_out1), .out2(decoder_2_out2), .out3(decoder_2_out3),
    .out4(decoder_2_out4), .out5(decoder_2_out5), .out6(decoder_2_out6), .out7(decoder_2_out7), .sel(IR[2:0]));
  or or_2 (or_2_out[0], decoder_2_out6, decoder_2_out5, decoder_2_out3, decoder_2_out2, decoder_2_out1, decoder_2_out0);
  or or_3 (or_2_out[1], decoder_2_out7, decoder_2_out6, decoder_2_out4, decoder_2_out2, decoder_2_out0);
  or or_4 (or_4_out[0], decoder_1_out6, decoder_1_out3, decoder_1_out1);
  or or_5 (or_4_out[1], RAMwrite, RAMload, decoder_1_out1);
  Multiplexer #(.select(3), .width(2), .enable("false")) multiplexer_6 (
    .in0(or_2_out), .in1(or_4_out), .in2(or_4_out), .in3(or_4_out), .in4(or_4_out), .in5(or_4_out),
    .in6(or_4_out), .in7(or_4_out), .out(Aluctrl[7:6]), .sel(IR[7:5]));
  or or_6 (Immsel, decoder_1_out1, RAMload, decoder_1_out3, RAMwrite);
  and and_2 (PCjr, or_7_out, decoder_1_out6);
  or or_7 (or_7_out, decoder_2_out1, decoder_2_out5);
  and and_3 (and_3_out, or_8_out, decoder_1_out6);
  or or_8 (or_8_out, decoder_2_out2, decoder_2_out4, decoder_2_out5, decoder_2_out6, decoder_2_out7);
  or or_9 (Regwrite, and_3_out, decoder_1_out0, decoder_1_out1, RAMload, decoder_1_out3);
  not not_3 (not_3_out[3], 1'b0);
  or or_10 (ALUenable, and_4_out, decoder_1_out0, decoder_1_out1, RAMload, decoder_1_out3, RAMwrite, PCselbeq);
  and and_4 (and_4_out, or_11_out, decoder_1_out6);
  or or_11 (or_11_out, decoder_2_out0, decoder_2_out1, decoder_2_out2, decoder_2_out4, decoder_2_out5);
  assign bit_extender_4_out = {{2{not_3_out[3]}}, not_3_out[3]};  // Bit_Extender bit_extender_4
  and and_5 (Disp, decoder_2_out0, decoder_1_out6);
  and and_6 (Inc, decoder_2_out7, decoder_1_out6);
  Multiplexer #(.select(3), .width(4), .enable("false")) multiplexer_7 (
    .in0({not_3_out[3], bit_extender_4_out}), .in1({not_3_out[3], bit_extender_4_out}),
    .in2({1'b0, bit_extender_4_out}), .in3({not_3_out[3], bit_extender_4_out}),
    .in4({1'b0, bit_extender_4_out}), .in5({not_3_out[3], bit_extender_4_out}),
    .in6({not_3_out[3], bit_extender_4_out}), .in7({not_3_out[3], bit_extender_4_out}),
    .out(multiplexer_7_out), .sel(IR[7:5]));
  assign Imm = multiplexer_7_out & IR[3:0];  // AND_Gate and_7, 4 bits wide

  assign Addr = IR[4:0];

  // Notes on the sheet:
  //   immd
  //   target addr
  //   funct code
  //   opcode
  //   rdg
  //   rxg
  //   opcode
  //   funct code
endmodule

module display (
  input  [1:0] Display_select,
  input  [7:0] in_2,
  input  Dispwrite,
  input  clock,
  input  reset,
  output [7:0] B,
  output [7:0] A,
  output [7:0] D,
  output [7:0] C,
  output [7:0] F,
  output [7:0] E,
  output [7:0] H,
  output [7:0] G
);

  wire demultiplexer_1_out0, demultiplexer_1_out1, demultiplexer_1_out2, demultiplexer_1_out3;
  wire [7:0] register_1_q, register_2_q, register_3_q, register_4_q;

  Demultiplexer #(.select(2), .enable("false")) demultiplexer_1 (
    .out0(demultiplexer_1_out0), .out1(demultiplexer_1_out1), .out2(demultiplexer_1_out2),
    .out3(demultiplexer_1_out3), .in(Dispwrite), .sel(Display_select));
  Register register_1 (.D(in_2), .en(demultiplexer_1_out0), .clk(clock), .Q(register_1_q), .clr(reset));
  Register register_2 (.D(in_2), .en(demultiplexer_1_out1), .clk(clock), .Q(register_2_q), .clr(reset));
  Register register_3 (.D(in_2), .en(demultiplexer_1_out2), .clk(clock), .Q(register_3_q), .clr(reset));
  Register register_4 (.D(in_2), .en(demultiplexer_1_out3), .clk(clock), .Q(register_4_q), .clr(reset));
  assign B = {{4{1'b0}}, register_1_q[3:0]};  // Bit_Extender bit_extender_1
  assign A = {{4{1'b0}}, register_1_q[7:4]};  // Bit_Extender bit_extender_2
  assign D = {{4{1'b0}}, register_2_q[3:0]};  // Bit_Extender bit_extender_3
  assign C = {{4{1'b0}}, register_2_q[7:4]};  // Bit_Extender bit_extender_4
  assign F = {{4{1'b0}}, register_3_q[3:0]};  // Bit_Extender bit_extender_5
  assign E = {{4{1'b0}}, register_3_q[7:4]};  // Bit_Extender bit_extender_6
  assign H = {{4{1'b0}}, register_4_q[3:0]};  // Bit_Extender bit_extender_7
  assign G = {{4{1'b0}}, register_4_q[7:4]};  // Bit_Extender bit_extender_8

  // Notes on the sheet:
  //   Display input
endmodule

module displayModule (
);

  wire blockbottom_1_out_5, blockbottom_1_out_6, blockbottom_1_out_7, blockbottom_1_out_8,
       blockbottom_1_out_9, blockbottom_1_out_10, blockbottom_1_out_11, blockbottom_1_out_12,
       blockbottom_1_out_13, blockbottom_1_out_14, blockbottom_1_out_15, blockbottom_1_out_16,
       blockbottom_1_out_17, blockbottom_1_out_18, blockbottom_1_out_19, blockbottom_1_out_20,
       blocktop_1_out_5, blocktop_1_out_6, blocktop_1_out_7, blocktop_1_out_8, blocktop_1_out_9,
       blocktop_1_out_10, blocktop_1_out_11, blocktop_1_out_12, blocktop_1_out_13, blocktop_1_out_14,
       blocktop_1_out_15, blocktop_1_out_16, blocktop_1_out_17, blocktop_1_out_18, blocktop_1_out_19,
       blocktop_1_out_20;
  wire [7:0] blackbox_1_out_5, blackbox_1_out_6, blackbox_1_out_7, blackbox_1_out_8, undriven, undriven_2,
       undriven_3, undriven_4;

  _7_Segment_Display u_7_segment_display_1 (
    .g(blocktop_1_out_5), .f(blocktop_1_out_13), .a(blocktop_1_out_14), .b(blocktop_1_out_6),
    .e(blockbottom_1_out_13), .d(blockbottom_1_out_5), .c(blockbottom_1_out_6), .dp(blockbottom_1_out_14));
  BlockBottom blockbottom_1 (
    .out_13(blockbottom_1_out_13), .out_5(blockbottom_1_out_5), .out_6(blockbottom_1_out_6),
    .out_14(blockbottom_1_out_14), .out_15(blockbottom_1_out_15), .out_7(blockbottom_1_out_7),
    .out_8(blockbottom_1_out_8), .out_16(blockbottom_1_out_16), .out_17(blockbottom_1_out_17),
    .out_9(blockbottom_1_out_9), .out_10(blockbottom_1_out_10), .out_18(blockbottom_1_out_18),
    .out_19(blockbottom_1_out_19), .out_11(blockbottom_1_out_11), .out_12(blockbottom_1_out_12),
    .out_20(blockbottom_1_out_20), .in_1(blackbox_1_out_5), .in_2(blackbox_1_out_6), .in_3(blackbox_1_out_7),
    .in_4(blackbox_1_out_8));
  BlockTop blocktop_1 (
    .in_1(blackbox_1_out_5), .in_2(blackbox_1_out_6), .in_3(blackbox_1_out_7), .in_4(blackbox_1_out_8),
    .out_5(blocktop_1_out_5), .out_13(blocktop_1_out_13), .out_14(blocktop_1_out_14),
    .out_6(blocktop_1_out_6), .out_7(blocktop_1_out_7), .out_15(blocktop_1_out_15),
    .out_16(blocktop_1_out_16), .out_8(blocktop_1_out_8), .out_9(blocktop_1_out_9),
    .out_17(blocktop_1_out_17), .out_18(blocktop_1_out_18), .out_10(blocktop_1_out_10),
    .out_11(blocktop_1_out_11), .out_19(blocktop_1_out_19), .out_20(blocktop_1_out_20),
    .out_12(blocktop_1_out_12));
  _7_Segment_Display u_7_segment_display_2 (
    .g(blocktop_1_out_9), .f(blocktop_1_out_17), .a(blocktop_1_out_18), .b(blocktop_1_out_10),
    .e(blockbottom_1_out_17), .d(blockbottom_1_out_9), .c(blockbottom_1_out_10), .dp(blockbottom_1_out_18));
  _7_Segment_Display u_7_segment_display_3 (
    .g(blocktop_1_out_7), .f(blocktop_1_out_15), .a(blocktop_1_out_16), .b(blocktop_1_out_8),
    .e(blockbottom_1_out_15), .d(blockbottom_1_out_7), .c(blockbottom_1_out_8), .dp(blockbottom_1_out_16));
  blackbox blackbox_1 (
    .out_5(blackbox_1_out_5), .out_6(blackbox_1_out_6), .out_7(blackbox_1_out_7), .out_8(blackbox_1_out_8),
    .in_1(undriven), .in_2(undriven_2), .in_3(undriven_3), .in_4(undriven_4));
  _7_Segment_Display u_7_segment_display_4 (
    .g(blocktop_1_out_11), .f(blocktop_1_out_19), .a(blocktop_1_out_20), .b(blocktop_1_out_12),
    .e(blockbottom_1_out_19), .d(blockbottom_1_out_11), .c(blockbottom_1_out_12), .dp(blockbottom_1_out_20));

  // Notes on the sheet:
  //   DISP[0]
  //   DISP[1]
endmodule

module Converter (
  input  [7:0] in_1,
  output out_2,
  output out_3,
  output out_4,
  output out_5,
  output out_6,
  output out_7,
  output out_8,
  output out_9
);

  wire and_1_out, or_1_out;
  wire [7:0] multiplexer_1_out, multiplexer_2_out;

  Multiplexer #(.select(4), .width(8), .enable("false")) multiplexer_1 (
    .in0(8'h77), .in1(8'h41), .in2(8'h3b), .in3(8'h6b), .in4(8'h4d), .in5(8'h6e), .in6(8'h7e), .in7(8'h43),
    .in8(8'h7f), .in9(8'h6f), .in10(8'h5f), .in11(8'h7c), .in12(8'h36), .in13(8'h79), .in14(8'h3e),
    .in15(8'h1e), .out(multiplexer_1_out), .sel(in_1[3:0]));
  or or_1 (or_1_out, in_1[4], in_1[5], in_1[6], in_1[7]);
  Multiplexer #(.width(8), .enable("false")) multiplexer_2 (
    .in0(multiplexer_1_out), .in1(8'h9b), .out(multiplexer_2_out), .sel(or_1_out));
  and and_1 (and_1_out, in_1[0], in_1[1], in_1[2], in_1[3], in_1[4], in_1[5], in_1[6], in_1[7]);
  Multiplexer #(.width(8), .enable("false")) multiplexer_3 (
    .in0(multiplexer_2_out), .in1({8{1'b0}}), .out({out_9, out_8, out_7, out_6, out_2, out_3, out_4, out_5}),
    .sel(and_1_out));

  // Notes on the sheet:
  //   0
  //   1
  //   2
  //   3
  //   4
  //   5
  //   6
  //   7
  //   8
  //   9
  //   a
  //   b
  //   c
  //   d
  //   e
  //   f
  //   ?
endmodule

module ConverterTop (
  input  [7:0] in_1,
  output out_2,
  output out_3,
  output out_4,
  output out_5
);

  wire and_1_out, or_1_out;
  wire [7:0] multiplexer_1_out, multiplexer_2_out;
  wire [7:4] multiplexer_3_out;

  Multiplexer #(.select(4), .width(8), .enable("false")) multiplexer_1 (
    .in0(8'h77), .in1(8'h41), .in2(8'h3b), .in3(8'h6b), .in4(8'h4d), .in5(8'h6e), .in6(8'h7e), .in7(8'h43),
    .in8(8'h7f), .in9(8'h6f), .in10(8'h5f), .in11(8'h7c), .in12(8'h36), .in13(8'h79), .in14(8'h3e),
    .in15(8'h1e), .out(multiplexer_1_out), .sel(in_1[3:0]));
  or or_1 (or_1_out, in_1[4], in_1[5], in_1[6], in_1[7]);
  Multiplexer #(.width(8), .enable("false")) multiplexer_2 (
    .in0(multiplexer_1_out), .in1(8'h9b), .out(multiplexer_2_out), .sel(or_1_out));
  and and_1 (and_1_out, in_1[0], in_1[1], in_1[2], in_1[3], in_1[4], in_1[5], in_1[6], in_1[7]);
  Multiplexer #(.width(8), .enable("false")) multiplexer_3 (
    .in0(multiplexer_2_out), .in1({8{1'b0}}), .out({multiplexer_3_out, out_2, out_3, out_4, out_5}),
    .sel(and_1_out));

  // Notes on the sheet:
  //   0
  //   1
  //   2
  //   3
  //   4
  //   5
  //   6
  //   7
  //   8
  //   9
  //   a
  //   b
  //   c
  //   d
  //   e
  //   f
  //   ?
endmodule

module ConverterBottom (
  input  [7:0] in_1,
  output out_2,
  output out_3,
  output out_4,
  output out_5
);

  wire and_1_out, or_1_out;
  wire [3:0] multiplexer_3_out;
  wire [7:0] multiplexer_1_out, multiplexer_2_out;

  Multiplexer #(.select(4), .width(8), .enable("false")) multiplexer_1 (
    .in0(8'h77), .in1(8'h41), .in2(8'h3b), .in3(8'h6b), .in4(8'h4d), .in5(8'h6e), .in6(8'h7e), .in7(8'h43),
    .in8(8'h7f), .in9(8'h6f), .in10(8'h5f), .in11(8'h7c), .in12(8'h36), .in13(8'h79), .in14(8'h3e),
    .in15(8'h1e), .out(multiplexer_1_out), .sel(in_1[3:0]));
  or or_1 (or_1_out, in_1[4], in_1[5], in_1[6], in_1[7]);
  Multiplexer #(.width(8), .enable("false")) multiplexer_2 (
    .in0(multiplexer_1_out), .in1(8'h9b), .out(multiplexer_2_out), .sel(or_1_out));
  and and_1 (and_1_out, in_1[0], in_1[1], in_1[2], in_1[3], in_1[4], in_1[5], in_1[6], in_1[7]);
  Multiplexer #(.width(8), .enable("false")) multiplexer_3 (
    .in0(multiplexer_2_out), .in1({8{1'b0}}), .out({out_5, out_4, out_3, out_2, multiplexer_3_out}),
    .sel(and_1_out));

  // Notes on the sheet:
  //   0
  //   1
  //   2
  //   3
  //   4
  //   5
  //   6
  //   7
  //   8
  //   9
  //   a
  //   b
  //   c
  //   d
  //   e
  //   f
  //   ?
endmodule

module blackbox (
  input  [7:0] in_1,
  input  [7:0] in_2,
  input  [7:0] in_3,
  input  [7:0] in_4,
  output [7:0] out_5,
  output [7:0] out_6,
  output [7:0] out_7,
  output [7:0] out_8
);


  assign out_5 = in_1;
  assign out_6 = in_2;
  assign out_7 = in_3;
  assign out_8 = in_4;
endmodule

module BlockTop (
  input  [7:0] in_1,
  input  [7:0] in_2,
  input  [7:0] in_3,
  input  [7:0] in_4,
  output out_5,
  output out_6,
  output out_7,
  output out_8,
  output out_9,
  output out_10,
  output out_11,
  output out_12,
  output out_13,
  output out_14,
  output out_15,
  output out_16,
  output out_17,
  output out_18,
  output out_19,
  output out_20
);

  ConverterTop convertertop_1 (.in_1(in_1), .out_2(out_5), .out_3(out_13), .out_4(out_14), .out_5(out_6));
  ConverterTop convertertop_2 (.in_1(in_2), .out_2(out_7), .out_3(out_15), .out_4(out_16), .out_5(out_8));
  ConverterTop convertertop_3 (.in_1(in_3), .out_2(out_9), .out_3(out_17), .out_4(out_18), .out_5(out_10));
  ConverterTop convertertop_4 (.in_1(in_4), .out_2(out_11), .out_3(out_19), .out_4(out_20), .out_5(out_12));
endmodule

module BlockBottom (
  input  [7:0] in_1,
  input  [7:0] in_2,
  input  [7:0] in_3,
  input  [7:0] in_4,
  output out_5,
  output out_6,
  output out_7,
  output out_8,
  output out_9,
  output out_10,
  output out_11,
  output out_12,
  output out_13,
  output out_14,
  output out_15,
  output out_16,
  output out_17,
  output out_18,
  output out_19,
  output out_20
);

  ConverterBottom converterbottom_1 (.in_1(in_1), .out_2(out_13), .out_3(out_5), .out_4(out_6), .out_5(out_14));
  ConverterBottom converterbottom_2 (.in_1(in_2), .out_2(out_15), .out_3(out_7), .out_4(out_8), .out_5(out_16));
  ConverterBottom converterbottom_3 (.in_1(in_3), .out_2(out_17), .out_3(out_9), .out_4(out_10), .out_5(out_18));
  ConverterBottom converterbottom_4 (.in_1(in_4), .out_2(out_19), .out_3(out_11), .out_4(out_12), .out_5(out_20));
endmodule
