// Logisim project adder_mux_lab.circ as structural Verilog: 2 circuits, main circuit adder_1bit
module adder_8bit (
  input  [7:0] A,
  input  Ctrl,
  input  [7:0] B,
  output [7:0] R,
  output Cout,
  output Oflw
);

  wire adder_1bit_1_cout, adder_1bit_2_cout, adder_1bit_3_cout, adder_1bit_4_cout, adder_1bit_5_cout,
       adder_1bit_6_cout, adder_1bit_7_cout, and_1_out, and_2_out, not_1_out, not_2_out, not_3_out,
       xor_1_out, xor_2_out, xor_3_out, xor_4_out, xor_5_out, xor_6_out, xor_7_out, xor_8_out;

  adder_1bit adder_1bit_1 (.A(A[0]), .B(xor_1_out), .Result(R[0]), .Cin(Ctrl), .Cout(adder_1bit_1_cout));
  xor xor_1 (xor_1_out, Ctrl, B[0]);
  adder_1bit adder_1bit_2 (.A(A[1]), .B(xor_2_out), .Result(R[1]), .Cin(adder_1bit_1_cout), .Cout(adder_1bit_2_cout));
  xor xor_2 (xor_2_out, Ctrl, B[1]);
  adder_1bit adder_1bit_3 (.A(A[2]), .B(xor_3_out), .Result(R[2]), .Cin(adder_1bit_2_cout), .Cout(adder_1bit_3_cout));
  xor xor_3 (xor_3_out, Ctrl, B[2]);
  adder_1bit adder_1bit_4 (.A(A[3]), .B(xor_4_out), .Result(R[3]), .Cin(adder_1bit_3_cout), .Cout(adder_1bit_4_cout));
  xor xor_4 (xor_4_out, Ctrl, B[3]);
  adder_1bit adder_1bit_5 (.A(A[4]), .B(xor_5_out), .Result(R[4]), .Cin(adder_1bit_4_cout), .Cout(adder_1bit_5_cout));
  xor xor_5 (xor_5_out, Ctrl, B[4]);
  adder_1bit adder_1bit_6 (.A(A[5]), .B(xor_6_out), .Result(R[5]), .Cin(adder_1bit_5_cout), .Cout(adder_1bit_6_cout));
  xor xor_6 (xor_6_out, Ctrl, B[5]);
  adder_1bit adder_1bit_7 (.A(A[6]), .B(xor_7_out), .Result(R[6]), .Cin(adder_1bit_6_cout), .Cout(adder_1bit_7_cout));
  xor xor_7 (xor_7_out, Ctrl, B[6]);
  adder_1bit adder_1bit_8 (.A(A[7]), .B(xor_8_out), .Result(R[7]), .Cin(adder_1bit_7_cout), .Cout(Cout));
  xor xor_8 (xor_8_out, Ctrl, B[7]);
  not not_1 (not_1_out, R[7]);
  not not_2 (not_2_out, xor_8_out);
  not not_3 (not_3_out, A[7]);
  and and_1 (and_1_out, not_1_out, xor_8_out, A[7]);
  and and_2 (and_2_out, R[7], not_2_out, not_3_out);
  or or_1 (Oflw, and_1_out, and_2_out);
endmodule

module adder_1bit (
  input  A,
  input  B,
  input  Cin,
  output Result,
  output Cout
);

  wire not_1_out, not_2_out;

  not not_1 (not_1_out, A);
  Multiplexer #(.select(2), .enable("false")) multiplexer_1 (
    .in0(A), .in1(not_1_out), .in2(not_1_out), .in3(A), .out(Result), .sel({B, Cin}));
  not not_2 (not_2_out, 1'b0);
  Multiplexer #(.select(2), .enable("false")) multiplexer_2 (
    .in0(1'b0), .in1(A), .in2(A), .in3(not_2_out), .out(Cout), .sel({B, Cin}));
endmodule
