// Logisim project shifter_lab.circ as structural Verilog: 1 circuit, main circuit main
module main (
  input  in_1,
  input  [7:0] X,
  input  [3:0] SUCtrl,
  input  [7:0] in_4,
  output [7:0] R,
  output ZF,
  output SF,
  output Ouflw
);

  wire and_1_out;
  wire [7:0] multiplexer_1_out;

  and and_1 (and_1_out, X[7], SUCtrl[2]);
  Multiplexer #(.select(2)) multiplexer_1 (
    .in0(in_1), .in1(X[1]), .in2(in_1), .in3(X[1]), .out(multiplexer_1_out[0]), .sel({SUCtrl[0], SUCtrl[1]}),
    .en(SUCtrl[3]));
  Multiplexer #(.select(2)) multiplexer_2 (
    .in0(X[0]), .in1(X[2]), .in2(in_1), .in3(X[2]), .out(multiplexer_1_out[1]), .sel({SUCtrl[0], SUCtrl[1]}),
    .en(SUCtrl[3]));
  Multiplexer #(.select(2)) multiplexer_3 (
    .in0(X[1]), .in1(X[3]), .in2(in_1), .in3(X[3]), .out(multiplexer_1_out[2]), .sel({SUCtrl[0], SUCtrl[1]}),
    .en(SUCtrl[3]));
  Multiplexer #(.select(2)) multiplexer_4 (
    .in0(X[2]), .in1(X[4]), .in2(in_1), .in3(X[4]), .out(multiplexer_1_out[3]), .sel({SUCtrl[0], SUCtrl[1]}),
    .en(SUCtrl[3]));
  Multiplexer #(.select(2)) multiplexer_5 (
    .in0(X[3]), .in1(X[5]), .in2(X[0]), .in3(X[5]), .out(multiplexer_1_out[4]), .sel({SUCtrl[0], SUCtrl[1]}),
    .en(SUCtrl[3]));
  Multiplexer #(.select(2)) multiplexer_6 (
    .in0(X[4]), .in1(X[6]), .in2(X[3]), .in3(X[6]), .out(multiplexer_1_out[5]), .sel({SUCtrl[0], SUCtrl[1]}),
    .en(SUCtrl[3]));
  Multiplexer #(.select(2)) multiplexer_7 (
    .in0(X[5]), .in1(X[7]), .in2(X[2]), .in3(X[7]), .out(multiplexer_1_out[6]), .sel({SUCtrl[0], SUCtrl[1]}),
    .en(SUCtrl[3]));
  Multiplexer #(.select(2)) multiplexer_8 (
    .in0(X[6]), .in1(and_1_out), .in2(X[3]), .in3(and_1_out), .out(multiplexer_1_out[7]),
    .sel({SUCtrl[0], SUCtrl[1]}), .en(SUCtrl[3]));
  Multiplexer #(.select(2), .width(8), .enable("false")) multiplexer_9 (
    .in0(X), .in1(X), .in2(multiplexer_1_out), .in3(multiplexer_1_out), .out(R), .sel({2{SUCtrl[3]}}));
  Comparator comparator_1 (.a(R), .b(in_4), .eq(ZF));  // open: gt, lt
  Comparator #(.width(1)) comparator_2 (.a(R[7]), .b(X[7]), .gt(Ouflw));  // open: eq, lt

  assign SF = R[7];
endmodule
