// Logisim project alu_lab.circ as structural Verilog: 7 circuits, main circuit alu
module alu (
  input  Enable,
  input  [7:0] AluCtrl,
  input  [7:0] A,
  input  [7:0] B,
  output [7:0] R,
  output ZF,
  output SF,
  output Oflw,
  output CF,
  output EQ
);

  wire adder_8bit_1_cout, adder_8bit_1_oflw, not_1_out, or_1_out;
  wire [7:0] adder_8bit_1_r, and_8bit_1_r, multiplexer_1_out, negator_1_out, or_8bit_1_r, shifter_8bit_1_r;

  and_8bit and_8bit_1 (.A(A), .B(B), .R(and_8bit_1_r));
  or_8bit or_8bit_1 (.A(A), .B(B), .R(or_8bit_1_r));
  adder_8bit adder_8bit_1 (
    .A(B), .B(A), .R(adder_8bit_1_r), .Cout(adder_8bit_1_cout), .Oflw(adder_8bit_1_oflw), .Ctrl(AluCtrl[5]));
  comparator_8bit comparator_8bit_1 (.R(EQ), .A(A), .B(B));
  Multiplexer #(.select(2), .width(8)) multiplexer_1 (
    .in0(and_8bit_1_r), .in1(or_8bit_1_r), .in2(negator_1_out), .in3(A), .out(multiplexer_1_out),
    .sel(AluCtrl[4:3]), .en(Enable));
  Negator negator_1 (.in(A), .out(negator_1_out));
  not not_1 (not_1_out, AluCtrl[6]);
  and and_1 (Oflw, not_1_out, AluCtrl[7], adder_8bit_1_oflw);
  and and_2 (CF, not_1_out, AluCtrl[7], adder_8bit_1_cout);
  shifter_8bit shifter_8bit_1 (.R(shifter_8bit_1_r), .A(A), .SUCtrl(AluCtrl[2:0]));
  Multiplexer #(.select(2), .width(8)) multiplexer_2 (
    .in0({8{1'b0}}), .in1(multiplexer_1_out), .in2(adder_8bit_1_r), .in3(shifter_8bit_1_r), .out(R),
    .sel(AluCtrl[7:6]), .en(Enable));
  or or_1 (or_1_out, R[0], R[1], R[2], R[3], R[4], R[5], R[6], R[7]);
  not not_2 (ZF, or_1_out);

  assign SF = R[7];
endmodule

module adder_1bit (
  input  Cin,
  input  A,
  input  B,
  output Result,
  output Cout
);

  wire and_1_out, and_2_out, xor_1_out;

  and and_1 (and_1_out, B, A);
  xor xor_1 (xor_1_out, A, B);
  and and_2 (and_2_out, xor_1_out, Cin);
  or or_1 (Cout, and_1_out, and_2_out);
  xor xor_2 (Result, Cin, xor_1_out);
endmodule

module adder_8bit (
  input  [7:0] A,
  input  Ctrl,
  input  [7:0] B,
  output [7:0] R,
  output Cout,
  output Oflw
);

  wire adder_1bit_1_cout, adder_1bit_2_cout, adder_1bit_3_cout, adder_1bit_4_cout, adder_1bit_5_cout,
       adder_1bit_6_cout, adder_1bit_7_cout, and_1_out, and_2_out, not_1_out, not_2_out, not_3_out,
       xor_1_out, xor_2_out, xor_3_out, xor_4_out, xor_5_out, xor_6_out, xor_7_out, xor_8_out;

  adder_1bit adder_1bit_1 (.A(A[0]), .B(xor_1_out), .Result(R[0]), .Cin(Ctrl), .Cout(adder_1bit_1_cout));
  xor xor_1 (xor_1_out, Ctrl, B[0]);
  adder_1bit adder_1bit_2 (.A(A[1]), .B(xor_2_out), .Result(R[1]), .Cin(adder_1bit_1_cout), .Cout(adder_1bit_2_cout));
  xor xor_2 (xor_2_out, Ctrl, B[1]);
  adder_1bit adder_1bit_3 (.A(A[2]), .B(xor_3_out), .Result(R[2]), .Cin(adder_1bit_2_cout), .Cout(adder_1bit_3_cout));
  xor xor_3 (xor_3_out, Ctrl, B[2]);
  adder_1bit adder_1bit_4 (.A(A[3]), .B(xor_4_out), .Result(R[3]), .Cin(adder_1bit_3_cout), .Cout(adder_1bit_4_cout));
  xor xor_4 (xor_4_out, Ctrl, B[3]);
  adder_1bit adder_1bit_5 (.A(A[4]), .B(xor_5_out), .Result(R[4]), .Cin(adder_1bit_4_cout), .Cout(adder_1bit_5_cout));
  xor xor_5 (xor_5_out, Ctrl, B[4]);
  adder_1bit adder_1bit_6 (.A(A[5]), .B(xor_6_out), .Result(R[5]), .Cin(adder_1bit_5_cout), .Cout(adder_1bit_6_cout));
  xor xor_6 (xor_6_out, Ctrl, B[5]);
  adder_1bit adder_1bit_7 (.A(A[6]), .B(xor_7_out), .Result(R[6]), .Cin(adder_1bit_6_cout), .Cout(adder_1bit_7_cout));
  xor xor_7 (xor_7_out, Ctrl, B[6]);
  adder_1bit adder_1bit_8 (.A(A[7]), .B(xor_8_out), .Result(R[7]), .Cin(adder_1bit_7_cout), .Cout(Cout));
  xor xor_8 (xor_8_out, Ctrl, B[7]);
  not not_1 (not_1_out, R[7]);
  not not_2 (not_2_out, xor_8_out);
  not not_3 (not_3_out, A[7]);
  and and_1 (and_1_out, not_1_out, xor_8_out, A[7]);
  and and_2 (and_2_out, R[7], not_2_out, not_3_out);
  or or_1 (Oflw, and_1_out, and_2_out);
endmodule

module and_8bit (
  input  [7:0] A,
  input  [7:0] B,
  output [7:0] R
);

  and and_1 (R[0], A[0], B[0]);
  and and_2 (R[1], A[1], B[1]);
  and and_3 (R[2], A[2], B[2]);
  and and_4 (R[3], A[3], B[3]);
  and and_5 (R[4], A[4], B[4]);
  and and_6 (R[5], A[5], B[5]);
  and and_7 (R[6], A[6], B[6]);
  and and_8 (R[7], A[7], B[7]);
endmodule

module or_8bit (
  input  [7:0] A,
  input  [7:0] B,
  output [7:0] R
);

  or or_1 (R[0], A[0], B[0]);
  or or_2 (R[1], A[1], B[1]);
  or or_3 (R[2], A[2], B[2]);
  or or_4 (R[3], A[3], B[3]);
  or or_5 (R[4], A[4], B[4]);
  or or_6 (R[5], A[5], B[5]);
  or or_7 (R[6], A[6], B[6]);
  or or_8 (R[7], A[7], B[7]);
endmodule

module shifter_8bit (
  input  [7:0] A,
  input  [2:0] SUCtrl,
  output [7:0] R
);

  wire multiplexer_1_out, multiplexer_3_out, multiplexer_5_out, multiplexer_7_out, multiplexer_8_out,
       multiplexer_11_out, multiplexer_13_out, multiplexer_15_out, not_1_out;

  not not_1 (not_1_out, 1'b0);
  Multiplexer #(.select(3), .enable("false")) multiplexer_1 (
    .in0(A[6]), .in1(A[3]), .in2(1'b0), .in3(1'b0), .in4(A[6]), .in5(A[3]), .in6(A[7]), .in7(A[7]),
    .out(multiplexer_1_out), .sel(SUCtrl));
  Multiplexer #(.enable("false")) multiplexer_2 (.in0(A[7]), .in1(multiplexer_1_out), .out(R[7]), .sel(not_1_out));
  Multiplexer #(.select(3), .enable("false")) multiplexer_3 (
    .in0(A[5]), .in1(A[2]), .in2(A[7]), .in3(A[7]), .in4(A[5]), .in5(A[2]), .in6(A[7]), .in7(A[7]),
    .out(multiplexer_3_out), .sel(SUCtrl));
  Multiplexer #(.enable("false")) multiplexer_4 (.in0(A[6]), .in1(multiplexer_3_out), .out(R[6]), .sel(not_1_out));
  Multiplexer #(.select(3), .enable("false")) multiplexer_5 (
    .in0(A[4]), .in1(A[1]), .in2(A[6]), .in3(A[6]), .in4(A[4]), .in5(A[1]), .in6(A[6]), .in7(A[6]),
    .out(multiplexer_5_out), .sel(SUCtrl));
  Multiplexer #(.enable("false")) multiplexer_6 (.in0(A[5]), .in1(multiplexer_5_out), .out(R[5]), .sel(not_1_out));
  Multiplexer #(.select(3), .enable("false")) multiplexer_7 (
    .in0(A[3]), .in1(A[0]), .in2(A[5]), .in3(A[5]), .in4(A[3]), .in5(A[0]), .in6(A[5]), .in7(A[5]),
    .out(multiplexer_7_out), .sel(SUCtrl));
  Multiplexer #(.select(3), .enable("false")) multiplexer_8 (
    .in0(A[2]), .in1(1'b0), .in2(A[4]), .in3(A[4]), .in4(A[2]), .in5(1'b0), .in6(A[4]), .in7(A[4]),
    .out(multiplexer_8_out), .sel(SUCtrl));
  Multiplexer #(.enable("false")) multiplexer_9 (.in0(A[4]), .in1(multiplexer_7_out), .out(R[4]), .sel(not_1_out));
  Multiplexer #(.enable("false")) multiplexer_10 (.in0(A[3]), .in1(multiplexer_8_out), .out(R[3]), .sel(not_1_out));
  Multiplexer #(.select(3), .enable("false")) multiplexer_11 (
    .in0(A[1]), .in1(1'b0), .in2(A[3]), .in3(A[3]), .in4(1'b0), .in5(1'b0), .in6(A[3]), .in7(A[3]),
    .out(multiplexer_11_out), .sel(SUCtrl));
  Multiplexer #(.enable("false")) multiplexer_12 (.in0(A[2]), .in1(multiplexer_11_out), .out(R[2]), .sel(not_1_out));
  Multiplexer #(.select(3), .enable("false")) multiplexer_13 (
    .in0(A[0]), .in1(1'b0), .in2(A[2]), .in3(A[2]), .in4(A[0]), .in5(1'b0), .in6(A[2]), .in7(A[2]),
    .out(multiplexer_13_out), .sel(SUCtrl));
  Multiplexer #(.enable("false")) multiplexer_14 (.in0(A[1]), .in1(multiplexer_13_out), .out(R[1]), .sel(not_1_out));
  Multiplexer #(.select(3), .enable("false")) multiplexer_15 (
    .in0(1'b0), .in1(1'b0), .in2(A[1]), .in3(A[1]), .in4(1'b0), .in5(1'b0), .in6(A[1]), .in7(A[1]),
    .out(multiplexer_15_out), .sel(SUCtrl));
  Multiplexer #(.enable("false")) multiplexer_16 (.in0(A[0]), .in1(multiplexer_15_out), .out(R[0]), .sel(not_1_out));
endmodule

module comparator_8bit (
  input  [7:0] A,
  input  [7:0] B,
  output R
);

  wire not_1_out, not_2_out, not_3_out, not_4_out, not_5_out, not_6_out, not_7_out, not_8_out, xor_1_out,
       xor_2_out, xor_3_out, xor_4_out, xor_5_out, xor_6_out, xor_7_out, xor_8_out;

  xor xor_1 (xor_1_out, A[0], B[0]);
  xor xor_2 (xor_2_out, A[1], B[1]);
  xor xor_3 (xor_3_out, A[2], B[2]);
  xor xor_4 (xor_4_out, A[3], B[3]);
  xor xor_5 (xor_5_out, A[4], B[4]);
  xor xor_6 (xor_6_out, A[5], B[5]);
  xor xor_7 (xor_7_out, A[6], B[6]);
  xor xor_8 (xor_8_out, A[7], B[7]);
  not not_1 (not_1_out, xor_1_out);
  not not_2 (not_2_out, xor_2_out);
  not not_3 (not_3_out, xor_3_out);
  not not_4 (not_4_out, xor_4_out);
  not not_5 (not_5_out, xor_5_out);
  not not_6 (not_6_out, xor_6_out);
  not not_7 (not_7_out, xor_7_out);
  not not_8 (not_8_out, xor_8_out);
  and and_1 (R, not_1_out, not_2_out, not_3_out, not_4_out, not_5_out, not_6_out, not_7_out, not_8_out);
endmodule
