// Logisim project ram_org_tg_lab.circ as structural Verilog: 4 circuits, main circuit adder_1bit
module testCircuit (
  input  Enable,
  input  Reset
);

  wire clock_1_out, comparator_1_eq, or_1_out, rom_3_p2, undriven;
  wire [7:0] adder_8bit_1_r, register_1_q;
  wire [15:0] ram_128kx16_1_dataout, rom_2_data;
  wire [20:0] rom_1_data;

  Clock clock_1 (.out(clock_1_out));
  Register #(.trigger("falling")) register_1 (
    .D(adder_8bit_1_r), .en(Enable), .clk(clock_1_out), .Q(register_1_q), .clr(or_1_out));
  or or_1 (or_1_out, Reset, comparator_1_eq);
  adder_8bit adder_8bit_1 (.A(register_1_q), .B(8'h1), .R(adder_8bit_1_r), .Ctrl(undriven));  // open: Cout, Oflw
  Comparator comparator_1 (.a(adder_8bit_1_r), .b(8'h21), .eq(comparator_1_eq));  // open: gt, lt
  ROM #(.dataWidth(21)) rom_1 (.addr(register_1_q), .data(rom_1_data));
  ROM #(.dataWidth(16)) rom_2 (.addr(register_1_q), .data(rom_2_data));
  // ROM #(.dataWidth(1)) rom_3: pin names not known; wires that end beside it: register_1_q, rom_3_p2
  ram_128kx16 ram_128kx16_1 (
    .datain(rom_2_data), .addr(rom_1_data), .clk(clock_1_out), .rw(rom_3_p2), .dataout(ram_128kx16_1_dataout));
  RAM #(.dataWidth(16), .trigger("falling"), .databus("bibus")) ram_1 (
    .addr(register_1_q), .we(Enable), .clk(clock_1_out), .din(ram_128kx16_1_dataout));  // open: oe, dout

  // Notes on the sheet:
  //   contents of rom_1 (hex, n*v repeats v):
  //   1235ab c0aad 7530a 167532 21b1f dcdef 198001 4700a 0 100000 c811f 456aa 144123 3a112 3456a bcdef
  //   1235ab c0aad 7530a 167532 21b1f dcdef 198001 4700a 0 100000 c811f 456aa 144123 3a112 3456a bcdef
  //   contents of rom_2 (hex, n*v repeats v):
  //   234a 2d57 680a 753a cdef 8947 56ac 8def ffff deaf 2948 cdfd d457 dfa9 fddf 8641
  //   contents of rom_3 (hex, n*v repeats v):
  //   16*1
endmodule

module ram_128kx16 (
  input  [15:0] datain,
  input  [20:0] addr,
  input  clk,
  input  rw,
  output [15:0] dataout
);

  wire and_1_out, and_2_out, and_4_out, decoder_1_out0, decoder_1_out1, decoder_1_out2, decoder_1_out3,
       decoder_2_out0, decoder_2_out1, decoder_2_out2, decoder_2_out3, not_1_out, not_2_out, not_3_out,
       not_4_out, not_5_out, not_6_out, not_7_out, not_9_out, transmission_1_p2, transmission_1_p3;
  wire [7:0] ram_1_dout, ram_2_dout, ram_3_dout, ram_4_dout, ram_5_dout, ram_6_dout, ram_7_dout, ram_8_dout,
       transmission_1_p4, transmission_5_p4;

  not not_1 (not_1_out, rw);
  Decoder #(.select(2)) decoder_1 (
    .out0(decoder_1_out0), .out1(decoder_1_out1), .out2(decoder_1_out2), .out3(decoder_1_out3),
    .sel(addr[20:19]), .en(not_1_out));
  Decoder #(.select(2)) decoder_2 (
    .out0(decoder_2_out0), .out1(decoder_2_out1), .out2(decoder_2_out2), .out3(decoder_2_out3),
    .sel(addr[20:19]), .en(rw));
  RAM #(.addrWidth(15), .databus("bibus")) ram_1 (
    .addr(addr[14:0]), .we(decoder_2_out0), .oe(decoder_1_out0), .clk(clk), .din(datain[7:0]),
    .dout(ram_1_dout));
  RAM #(.addrWidth(15), .databus("bibus")) ram_2 (
    .addr(addr[14:0]), .we(decoder_2_out1), .oe(decoder_1_out1), .clk(clk), .din(datain[7:0]),
    .dout(ram_2_dout));
  RAM #(.addrWidth(15), .databus("bibus")) ram_3 (
    .addr(addr[14:0]), .we(decoder_2_out2), .oe(decoder_1_out2), .clk(clk), .din(datain[7:0]),
    .dout(ram_3_dout));
  RAM #(.addrWidth(15), .databus("bibus")) ram_4 (
    .addr(addr[14:0]), .we(decoder_2_out3), .oe(decoder_1_out3), .clk(clk), .din(datain[7:0]),
    .dout(ram_4_dout));
  not not_2 (not_2_out, addr[19]);
  not not_3 (not_3_out, addr[20]);
  // Transmission_Gate #(.width(8)) transmission_1: pin names not known; wires that end beside it: ram_3_dout, transmission_1_p2, transmission_1_p3, transmission_1_p4
  not not_4 (not_4_out, and_4_out);
  and and_1 (and_1_out, not_3_out, not_2_out);
  not not_5 (not_5_out, and_1_out);
  // Transmission_Gate #(.width(8)) transmission_2: pin names not known; wires that end beside it: ram_1_dout, not_5_out, and_1_out, transmission_1_p4
  not not_6 (not_6_out, addr[20]);
  and and_2 (and_2_out, not_6_out, addr[19]);
  not not_7 (not_7_out, and_2_out);
  // Transmission_Gate #(.width(8)) transmission_3: pin names not known; wires that end beside it: ram_2_dout, not_7_out, and_2_out, transmission_1_p4
  and and_3 (transmission_1_p3, addr[20], not_9_out);
  not not_8 (transmission_1_p2, transmission_1_p3);
  and and_4 (and_4_out, addr[20], addr[19]);
  // Transmission_Gate #(.width(8)) transmission_4: pin names not known; wires that end beside it: ram_4_dout, not_4_out, and_4_out, transmission_1_p4
  not not_9 (not_9_out, addr[19]);
  RAM #(.addrWidth(15), .databus("bibus")) ram_5 (
    .addr(addr[14:0]), .we(decoder_2_out0), .oe(decoder_1_out0), .clk(clk), .din(datain[15:8]),
    .dout(ram_5_dout));
  RAM #(.addrWidth(15), .databus("bibus")) ram_6 (
    .addr(addr[14:0]), .we(decoder_2_out1), .oe(decoder_1_out1), .clk(clk), .din(datain[15:8]),
    .dout(ram_6_dout));
  RAM #(.addrWidth(15), .databus("bibus")) ram_7 (
    .addr(addr[14:0]), .we(decoder_2_out2), .oe(decoder_1_out2), .clk(clk), .din(datain[15:8]),
    .dout(ram_7_dout));
  RAM #(.addrWidth(15), .databus("bibus")) ram_8 (
    .addr(addr[14:0]), .we(decoder_2_out3), .oe(decoder_1_out3), .clk(clk), .din(datain[15:8]),
    .dout(ram_8_dout));
  // Transmission_Gate #(.width(8)) transmission_5: pin names not known; wires that end beside it: ram_5_dout, not_5_out, and_1_out, transmission_5_p4
  // Transmission_Gate #(.width(8)) transmission_6: pin names not known; wires that end beside it: ram_6_dout, not_7_out, and_2_out, transmission_5_p4
  // Transmission_Gate #(.width(8)) transmission_7: pin names not known; wires that end beside it: ram_7_dout, transmission_1_p2, transmission_1_p3, transmission_5_p4
  // Transmission_Gate #(.width(8)) transmission_8: pin names not known; wires that end beside it: ram_8_dout, not_4_out, and_4_out, transmission_5_p4
  Multiplexer #(.width(16), .enable("false")) multiplexer_1 (
    .in0({16{1'b0}}), .in1({transmission_5_p4, transmission_1_p4}), .out(dataout), .sel(not_1_out));
endmodule

module adder_1bit (
  input  Cin,
  input  A,
  input  B,
  output Result,
  output Cout
);

  wire and_1_out, and_2_out, xor_1_out;

  and and_1 (and_1_out, B, A);
  xor xor_1 (xor_1_out, A, B);
  and and_2 (and_2_out, xor_1_out, Cin);
  or or_1 (Cout, and_1_out, and_2_out);
  xor xor_2 (Result, Cin, xor_1_out);
endmodule

module adder_8bit (
  input  [7:0] A,
  input  Ctrl,
  input  [7:0] B,
  output [7:0] R,
  output Cout,
  output Oflw
);

  wire adder_1bit_1_cout, adder_1bit_2_cout, adder_1bit_3_cout, adder_1bit_4_cout, adder_1bit_5_cout,
       adder_1bit_6_cout, adder_1bit_7_cout, and_1_out, and_2_out, not_1_out, not_2_out, not_3_out,
       xor_1_out, xor_2_out, xor_3_out, xor_4_out, xor_5_out, xor_6_out, xor_7_out, xor_8_out;

  adder_1bit adder_1bit_1 (.A(A[0]), .B(xor_1_out), .Result(R[0]), .Cin(Ctrl), .Cout(adder_1bit_1_cout));
  xor xor_1 (xor_1_out, Ctrl, B[0]);
  adder_1bit adder_1bit_2 (.A(A[1]), .B(xor_2_out), .Result(R[1]), .Cin(adder_1bit_1_cout), .Cout(adder_1bit_2_cout));
  xor xor_2 (xor_2_out, Ctrl, B[1]);
  adder_1bit adder_1bit_3 (.A(A[2]), .B(xor_3_out), .Result(R[2]), .Cin(adder_1bit_2_cout), .Cout(adder_1bit_3_cout));
  xor xor_3 (xor_3_out, Ctrl, B[2]);
  adder_1bit adder_1bit_4 (.A(A[3]), .B(xor_4_out), .Result(R[3]), .Cin(adder_1bit_3_cout), .Cout(adder_1bit_4_cout));
  xor xor_4 (xor_4_out, Ctrl, B[3]);
  adder_1bit adder_1bit_5 (.A(A[4]), .B(xor_5_out), .Result(R[4]), .Cin(adder_1bit_4_cout), .Cout(adder_1bit_5_cout));
  xor xor_5 (xor_5_out, Ctrl, B[4]);
  adder_1bit adder_1bit_6 (.A(A[5]), .B(xor_6_out), .Result(R[5]), .Cin(adder_1bit_5_cout), .Cout(adder_1bit_6_cout));
  xor xor_6 (xor_6_out, Ctrl, B[5]);
  adder_1bit adder_1bit_7 (.A(A[6]), .B(xor_7_out), .Result(R[6]), .Cin(adder_1bit_6_cout), .Cout(adder_1bit_7_cout));
  xor xor_7 (xor_7_out, Ctrl, B[6]);
  adder_1bit adder_1bit_8 (.A(A[7]), .B(xor_8_out), .Result(R[7]), .Cin(adder_1bit_7_cout), .Cout(Cout));
  xor xor_8 (xor_8_out, Ctrl, B[7]);
  not not_1 (not_1_out, R[7]);
  not not_2 (not_2_out, xor_8_out);
  not not_3 (not_3_out, A[7]);
  and and_1 (and_1_out, not_1_out, xor_8_out, A[7]);
  and and_2 (and_2_out, R[7], not_2_out, not_3_out);
  or or_1 (Oflw, and_1_out, and_2_out);
endmodule
