// Logisim project registers_file_lab.circ as structural Verilog: 2 circuits, main circuit regs_4x8
module testCircuit (
  input  Enable,
  input  Reset
);

  wire clock_1_out, comparator_1_eq, or_1_out, rom_3_p2;
  wire [7:0] adder_1_out, register_1_q, regs_4x8_1_dataouta, regs_4x8_1_dataoutb, rom_1_data, rom_2_data;

  Clock clock_1 (.out(clock_1_out));
  Register #(.trigger("falling")) register_1 (
    .D(adder_1_out), .en(Enable), .clk(clock_1_out), .Q(register_1_q), .clr(or_1_out));
  or or_1 (or_1_out, Reset, comparator_1_eq);
  Adder adder_1 (.a(register_1_q), .b(8'h1), .out(adder_1_out));  // open: cin, cout
  Comparator comparator_1 (.a(adder_1_out), .b(8'h21), .eq(comparator_1_eq));  // open: gt, lt
  ROM rom_1 (.addr(register_1_q), .data(rom_1_data));
  ROM rom_2 (.addr(register_1_q), .data(rom_2_data));
  // ROM #(.dataWidth(1)) rom_3: pin names not known; wires that end beside it: register_1_q, rom_3_p2
  regs_4x8 regs_4x8_1 (
    .Datain(rom_2_data), .WriteEnable(rom_3_p2), .DataoutA(regs_4x8_1_dataouta),
    .DataoutB(regs_4x8_1_dataoutb), .DestReg(rom_1_data[5:4]), .OutBsel(rom_1_data[3:2]),
    .OutAsel(rom_1_data[1:0]), .Clock(clock_1_out), .Clear(Reset));
  RAM #(.dataWidth(16), .trigger("falling"), .databus("bibus")) ram_1 (
    .addr(register_1_q), .we(Enable), .clk(clock_1_out), .din({regs_4x8_1_dataoutb, regs_4x8_1_dataouta}));  // open: oe, dout

  // Notes on the sheet:
  //   contents of rom_1 (hex, n*v repeats v):
  //   ab ad a 32 1f ef 1 a 0 0 1f aa 23 12 6a ef ab ad a 32 1f ef 1 a 0 0 1f aa 23 12 6a ef
  //   contents of rom_2 (hex, n*v repeats v):
  //   4a 57 a 3a ef 47 ac ef ff af 48 fd 57 a9 df 41 ab ff ee cd 43 77 68 90 a1 45 56 0 89 32 fd da
  //   contents of rom_3 (hex, n*v repeats v):
  //   4*1 4*0 4*1 4*0 4*1 4*0 4*1
endmodule

module regs_4x8 (
  input  [1:0] DestReg,
  input  [1:0] OutBsel,
  input  [1:0] OutAsel,
  input  [7:0] Datain,
  input  WriteEnable,
  input  Clock,
  input  Clear,
  output [7:0] DataoutA,
  output [7:0] DataoutB
);

  wire demultiplexer_1_out0, demultiplexer_1_out1, demultiplexer_1_out2, demultiplexer_1_out3;
  wire [7:0] register_1_q, register_2_q, register_3_q, register_4_q;

  Demultiplexer #(.select(2), .enable("false")) demultiplexer_1 (
    .out0(demultiplexer_1_out0), .out1(demultiplexer_1_out1), .out2(demultiplexer_1_out2),
    .out3(demultiplexer_1_out3), .in(WriteEnable), .sel(DestReg));
  Register register_1 (.D(Datain), .en(demultiplexer_1_out0), .clk(Clock), .Q(register_1_q), .clr(Clear));
  Register register_2 (.D(Datain), .en(demultiplexer_1_out1), .clk(Clock), .Q(register_2_q), .clr(Clear));
  Register register_3 (.D(Datain), .en(demultiplexer_1_out2), .clk(Clock), .Q(register_3_q), .clr(Clear));
  Register register_4 (.D(Datain), .en(demultiplexer_1_out3), .clk(Clock), .Q(register_4_q), .clr(Clear));
  Multiplexer #(.select(2), .width(8), .enable("false")) multiplexer_1 (
    .in0(register_1_q), .in1(register_2_q), .in2(register_3_q), .in3(register_4_q), .out(DataoutA),
    .sel(OutAsel));
  Multiplexer #(.select(2), .width(8), .enable("false")) multiplexer_2 (
    .in0(register_1_q), .in1(register_2_q), .in2(register_3_q), .in3(register_4_q), .out(DataoutB),
    .sel(OutBsel));
endmodule
