// Logisim project fetch_lab 1.circ as structural Verilog: 4 circuits, main circuit adder_1bit
module testCircuit (
  input  Load,
  input  Reset
);

  wire clock_1_out, comparator_1_eq, comparator_2_eq, comparator_3_eq, Eq, or_1_out, or_2_out, or_3_out,
       register_3_q, selbeq, seljmp, seljr, undriven, undriven_2, undriven_3;
  wire [4:0] Addrin;
  wire [7:0] adder_8bit_1_r, adder_8bit_2_r, adder_8bit_3_r, instfetcher_1_nextpc, multiplexer_1_out,
       Regaddrin, register_1_q, register_2_q, register_4_q;
  wire [23:5] rom_1_data;

  Register #(.trigger("falling")) register_1 (
    .D(adder_8bit_1_r), .en(Load), .clk(clock_1_out), .Q(register_1_q), .clr(or_1_out));
  or or_1 (or_1_out, Reset, comparator_1_eq);
  adder_8bit adder_8bit_1 (.A(register_1_q), .B(8'h1), .R(adder_8bit_1_r), .Ctrl(undriven));  // open: Cout, Oflw
  Comparator comparator_1 (.a(adder_8bit_1_r), .b(8'h1c), .eq(comparator_1_eq));  // open: gt, lt
  ROM #(.dataWidth(24)) rom_1 (
    .addr(register_1_q),
    .data({rom_1_data[23:20], Eq, selbeq, seljmp, seljr, Regaddrin, rom_1_data[7:5], Addrin}));
  instFetcher instfetcher_1 (
    .Addr(Addrin), .PCselbeq(selbeq), .Clock(clock_1_out), .Clr(rom_1_data[20]), .PCseljmp(seljmp), .Eq(Eq),
    .PCLoad(Load), .IRLoad(Load), .NextPC(instfetcher_1_nextpc), .PCseljr(seljr), .Regaddr(Regaddrin));  // open: Instruction
  Clock clock_1 (.out(clock_1_out));
  Register #(.trigger("falling")) register_2 (
    .D(adder_8bit_2_r), .en(Load), .clk(clock_1_out), .Q(register_2_q), .clr(or_2_out));
  or or_2 (or_2_out, Reset, register_3_q);
  adder_8bit adder_8bit_2 (.A(register_2_q), .B(8'h1), .R(adder_8bit_2_r), .Ctrl(undriven_2));  // open: Cout, Oflw
  Comparator comparator_2 (.a(register_2_q), .b(8'h2), .eq(comparator_2_eq));  // open: gt, lt
  Register #(.width(1)) register_3 (.D(comparator_2_eq), .en(Load), .clk(clock_1_out), .Q(register_3_q), .clr(Reset));
  Register #(.trigger("falling")) register_4 (
    .D(adder_8bit_3_r), .en(Load), .clk(clock_1_out), .Q(register_4_q), .clr(or_3_out));
  RAM #(.trigger("falling"), .databus("bibus")) ram_1 (
    .addr(register_4_q), .we(register_3_q), .clk(clock_1_out), .din(instfetcher_1_nextpc));  // open: oe, dout
  Multiplexer #(.width(8), .enable("false")) multiplexer_1 (
    .in0({8{1'b0}}), .in1(8'h1), .out(multiplexer_1_out), .sel(register_3_q));
  adder_8bit adder_8bit_3 (
    .A(register_4_q), .B(multiplexer_1_out), .R(adder_8bit_3_r), .Ctrl(undriven_3));  // open: Cout, Oflw
  or or_3 (or_3_out, Reset, comparator_3_eq);
  Comparator comparator_3 (.a(adder_8bit_3_r), .b(8'ha), .eq(comparator_3_eq));  // open: gt, lt

  // Notes on the sheet:
  //   contents of rom_1 (hex, n*v repeats v):
  //   100000 4c0a 0 100000 21b1f 0 100000 4700a 0 100000 c811f 0 100000 123a1 0 100000 26a00 0 100000
  //   c7505 0 100000 18200 0 100000 2001f
endmodule

module instFetcher (
  input  Eq,
  input  PCselbeq,
  input  PCseljmp,
  input  PCseljr,
  input  PCLoad,
  input  IRLoad,
  input  [4:0] Addr,
  input  [7:0] Regaddr,
  input  Clock,
  input  Clr,
  output [7:0] NextPC,
  output [7:0] Instruction
);

  wire not_1_out;
  wire [7:0] adder_8bit_1_r, bit_extender_1_out, bit_extender_2_out, multiplexer_1_out, multiplexer_2_out,
       multiplexer_3_out, register_1_q, rom_1_data;

  not not_1 (not_1_out, 1'b0);
  assign bit_extender_1_out = {{7{1'b0}}, not_1_out};  // Bit_Extender bit_extender_1
  assign bit_extender_2_out = {{3{Addr[4]}}, Addr};  // Bit_Extender bit_extender_2
  adder_8bit adder_8bit_1 (.A(bit_extender_2_out), .B(NextPC), .R(adder_8bit_1_r), .Ctrl(1'b0));  // open: Cout, Oflw
  Multiplexer #(.select(2), .width(8), .enable("false")) multiplexer_1 (
    .in0(bit_extender_1_out), .in1(bit_extender_1_out), .in2(adder_8bit_1_r), .in3(adder_8bit_1_r),
    .out(multiplexer_1_out), .sel({Eq, PCselbeq}));
  Multiplexer #(.width(8), .enable("false")) multiplexer_2 (
    .in0(multiplexer_1_out), .in1({NextPC[7:5], Addr}), .out(multiplexer_2_out), .sel(PCseljmp));
  Multiplexer #(.width(8), .enable("false")) multiplexer_3 (
    .in0(multiplexer_2_out), .in1(Regaddr), .out(multiplexer_3_out), .sel(PCseljr));
  Register #(.trigger("falling")) register_1 (
    .D(multiplexer_3_out), .en(PCLoad), .clk(Clock), .Q(register_1_q), .clr(Clr));
  adder_8bit adder_8bit_2 (.A(register_1_q), .B(bit_extender_1_out), .R(NextPC), .Ctrl(1'b0));  // open: Cout, Oflw
  ROM rom_1 (.addr(register_1_q), .data(rom_1_data));
  Register register_2 (.D(rom_1_data), .en(IRLoad), .clk(Clock), .Q(Instruction), .clr(Clr));

  // Notes on the sheet:
  //   contents of rom_1 (hex, n*v repeats v):
  //   43 6f 53 7f ff 1 2 3 4 5 6 7 8 9 10 1a 1b 1c 1d 1e 1f 20 21 22 23 24 24 26 27 28 29 30 31 32 33 34
  //   35 36 37 38 39 3a 3b 3c 3d 3e 3f 40 41 42 43 44 45 46 47 48 49 50 51 52 53 54 55 56 57 58 59 60 61
  //   62 63 64 65 66 67 68 69 70 71 72 73 74 75 76 77 78 79 80 81 82 83 84 85 86 87 88 89 8a 8b 8c 8d 8e
  //   8f 90 91 92 93 94 95 96 97 98 99 9a 9b 9c 9d 9e 9f a0 a1 a2 a3 a4 a5 a6 a7 a8 a9 aa ab ac ad ae af
  //   b0 b1 b2 b3 b4 b5 b6 b7 b8 b9 ba bb bc bd be bf c0 c1 c2 c3 c4 c5 c6 c7 c8 c9 ca cb cd ce cf d0
endmodule

module adder_1bit (
  input  Cin,
  input  A,
  input  B,
  output Result,
  output Cout
);

  wire and_1_out, and_2_out, xor_1_out;

  and and_1 (and_1_out, B, A);
  xor xor_1 (xor_1_out, A, B);
  and and_2 (and_2_out, xor_1_out, Cin);
  or or_1 (Cout, and_1_out, and_2_out);
  xor xor_2 (Result, Cin, xor_1_out);
endmodule

module adder_8bit (
  input  [7:0] A,
  input  Ctrl,
  input  [7:0] B,
  output [7:0] R,
  output Cout,
  output Oflw
);

  wire adder_1bit_1_cout, adder_1bit_2_cout, adder_1bit_3_cout, adder_1bit_4_cout, adder_1bit_5_cout,
       adder_1bit_6_cout, adder_1bit_7_cout, and_1_out, and_2_out, not_1_out, not_2_out, not_3_out,
       xor_1_out, xor_2_out, xor_3_out, xor_4_out, xor_5_out, xor_6_out, xor_7_out, xor_8_out;

  adder_1bit adder_1bit_1 (.A(A[0]), .B(xor_1_out), .Result(R[0]), .Cin(Ctrl), .Cout(adder_1bit_1_cout));
  xor xor_1 (xor_1_out, Ctrl, B[0]);
  adder_1bit adder_1bit_2 (.A(A[1]), .B(xor_2_out), .Result(R[1]), .Cin(adder_1bit_1_cout), .Cout(adder_1bit_2_cout));
  xor xor_2 (xor_2_out, Ctrl, B[1]);
  adder_1bit adder_1bit_3 (.A(A[2]), .B(xor_3_out), .Result(R[2]), .Cin(adder_1bit_2_cout), .Cout(adder_1bit_3_cout));
  xor xor_3 (xor_3_out, Ctrl, B[2]);
  adder_1bit adder_1bit_4 (.A(A[3]), .B(xor_4_out), .Result(R[3]), .Cin(adder_1bit_3_cout), .Cout(adder_1bit_4_cout));
  xor xor_4 (xor_4_out, Ctrl, B[3]);
  adder_1bit adder_1bit_5 (.A(A[4]), .B(xor_5_out), .Result(R[4]), .Cin(adder_1bit_4_cout), .Cout(adder_1bit_5_cout));
  xor xor_5 (xor_5_out, Ctrl, B[4]);
  adder_1bit adder_1bit_6 (.A(A[5]), .B(xor_6_out), .Result(R[5]), .Cin(adder_1bit_5_cout), .Cout(adder_1bit_6_cout));
  xor xor_6 (xor_6_out, Ctrl, B[5]);
  adder_1bit adder_1bit_7 (.A(A[6]), .B(xor_7_out), .Result(R[6]), .Cin(adder_1bit_6_cout), .Cout(adder_1bit_7_cout));
  xor xor_7 (xor_7_out, Ctrl, B[6]);
  adder_1bit adder_1bit_8 (.A(A[7]), .B(xor_8_out), .Result(R[7]), .Cin(adder_1bit_7_cout), .Cout(Cout));
  xor xor_8 (xor_8_out, Ctrl, B[7]);
  not not_1 (not_1_out, R[7]);
  not not_2 (not_2_out, xor_8_out);
  not not_3 (not_3_out, A[7]);
  and and_1 (and_1_out, not_1_out, xor_8_out, A[7]);
  and and_2 (and_2_out, R[7], not_2_out, not_3_out);
  or or_1 (Oflw, and_1_out, and_2_out);
endmodule
